// Logisim project MiniMips32.circ as structural Verilog
module MiniMips32 (
  input  rst
);

  wire clk_out, emreg, exe_1_exe2id_wreg, exe_1_exe_mreg_o, exe_1_exe_whilo_o, exe_1_exe_wreg_o,
       exemem_reg_1_mem_mreg, exemem_reg_1_mem_whilo, exemem_reg_1_mem_wreg, id_1_id_mreg_o, id_1_id_whilo_o,
       id_1_id_wreg_o, id_1_rreg1, id_1_rreg2, idexe_reg_1_exe_mreg, idexe_reg_1_exe_whilo,
       idexe_reg_1_exe_wreg, if_1_ice, mem_1_dce, mem_1_mem2id_wreg, mem_1_mem_mreg_o, mem_1_mem_whilo_o,
       mem_1_mem_wreg_o, memwb_reg_1_wb_mreg, memwb_reg_1_wb_whilo, memwb_reg_1_wb_wreg, mmreg, stallreq_exe,
       stallreq_id, wb_1_wb_whilo_o, wb_1_wb_wreg_o;
  wire [1:0] id_1_jtsel, mem_1_mem2exe_whilo;
  wire [2:0] id_1_id_alutype_o, idexe_reg_1_exe_alutype;
  wire [3:0] mem_1_dre, mem_1_we, memwb_reg_1_wb_dre, stall;
  wire [4:0] exe_1_exe2id_wa, exe_1_exe_wa_o, exemem_reg_1_mem_wa, id_1_id_wa_o, id_1_ra1, id_1_ra2,
       idexe_reg_1_exe_wa, mem_1_mem2id_wa, mem_1_mem_wa_o, memwb_reg_1_wb_wa, wb_1_wb_wa_o;
  wire [7:0] exe_1_exe_aluop_o, exemem_reg_1_mem_aluop, id_1_id_aluop_o, idexe_reg_1_exe_aluop;
  wire [23:0] if_1_iaddr, mem_1_daddr;
  wire [31:0] dm_1_dout, exe_1_exe2id_wd, exe_1_exe_din_o, exe_1_exe_hi_o, exe_1_exe_lo_o, exe_1_exe_wd_o,
       exemem_reg_1_mem_din, exemem_reg_1_mem_hi, exemem_reg_1_mem_lo, exemem_reg_1_mem_wd, hilo_1_out_5,
       hilo_1_out_6, id_1_addr1, id_1_addr2, id_1_addr3, id_1_id_din_o, id_1_id_src1_o, id_1_id_src2_o,
       id_1_ret_addr, idexe_reg_1_exe_din, idexe_reg_1_exe_ret_addr, idexe_reg_1_exe_src1,
       idexe_reg_1_exe_src2, if_1_pc, ifid_reg_1_id_inst, ifid_reg_1_id_pc, im_1_inst, mem_1_din,
       mem_1_mem2exe_hi, mem_1_mem2exe_lo, mem_1_mem2id_wd, mem_1_mem_dreg_o, mem_1_mem_hi_o, mem_1_mem_lo_o,
       memwb_reg_1_wb_dm, memwb_reg_1_wb_dreg, memwb_reg_1_wb_hi, memwb_reg_1_wb_lo, multiplexer_1_out,
       multiplexer_2_out, regfile_1_rd1, regfile_1_rd2, wb_1_wb2exe_hi, wb_1_wb2exe_lo, wb_1_wb_hi_o,
       wb_1_wb_lo_o, wb_1_wb_wd_o;

  Clock clk (.out(clk_out));
  \if  if_1 (
    .clk(clk_out), .pc(if_1_pc), .iaddr(if_1_iaddr), .ice(if_1_ice), .rst(rst), .addr1(id_1_addr1),
    .addr2(id_1_addr2), .addr3(id_1_addr3), .jtsel(id_1_jtsel), .stall(stall));
  IM im_1 (.iaddr(if_1_iaddr), .ice(if_1_ice), .inst(im_1_inst));
  ifid_reg ifid_reg_1 (
    .if_pc(if_1_pc), .rst(rst), .clk(clk_out), .id_pc(ifid_reg_1_id_pc), .if_inst(im_1_inst),
    .id_inst(ifid_reg_1_id_inst), .stall(stall));
  RegFile regfile_1 (
    .we(wb_1_wb_wreg_o), .ra1(id_1_ra1), .ra2(id_1_ra2), .rd1(regfile_1_rd1), .wa(wb_1_wb_wa_o),
    .rd2(regfile_1_rd2), .wd(wb_1_wb_wd_o), .clk(clk_out), .re1(id_1_rreg1), .re1_2(id_1_rreg2));
  id id_1 (
    .id_inst_i(ifid_reg_1_id_inst), .rd1(regfile_1_rd1), .rd2(regfile_1_rd2), .rst(rst),
    .id_mreg_o(id_1_id_mreg_o), .id_whilo_o(id_1_id_whilo_o), .id_wreg_o(id_1_id_wreg_o),
    .id_alutype_o(id_1_id_alutype_o), .id_aluop_o(id_1_id_aluop_o), .id_wa_o(id_1_id_wa_o),
    .id_src1_o(id_1_id_src1_o), .ra1(id_1_ra1), .ra2(id_1_ra2), .id_src2_o(id_1_id_src2_o),
    .id_din_o(id_1_id_din_o), .rreg1(id_1_rreg1), .rreg2(id_1_rreg2), .exe2id_wa(exe_1_exe2id_wa),
    .mem2id_wa(mem_1_mem2id_wa), .exe2id_wreg(exe_1_exe2id_wreg), .mem2id_wreg(mem_1_mem2id_wreg),
    .exe2id_wd(exe_1_exe2id_wd), .mem2id_wd(mem_1_mem2id_wd), .jtsel(id_1_jtsel), .addr1(id_1_addr1),
    .addr3(id_1_addr3), .addr2(id_1_addr2), .id_pc_i(ifid_reg_1_id_pc), .ret_addr(id_1_ret_addr),
    .stallreq_id(stallreq_id), .exe2id_mreg(emreg), .mem2id_mreg(mmreg));
  idexe_reg idexe_reg_1 (
    .id_mreg(id_1_id_mreg_o), .id_whilo(id_1_id_whilo_o), .id_wreg(id_1_id_wreg_o),
    .id_alutype(id_1_id_alutype_o), .id_aluop(id_1_id_aluop_o), .id_wa(id_1_id_wa_o),
    .id_src1(id_1_id_src1_o), .id_src2(id_1_id_src2_o), .id_din(id_1_id_din_o),
    .exe_mreg(idexe_reg_1_exe_mreg), .exe_whilo(idexe_reg_1_exe_whilo), .exe_wreg(idexe_reg_1_exe_wreg),
    .exe_alutype(idexe_reg_1_exe_alutype), .exe_aluop(idexe_reg_1_exe_aluop), .exe_wa(idexe_reg_1_exe_wa),
    .exe_src1(idexe_reg_1_exe_src1), .exe_src2(idexe_reg_1_exe_src2), .exe_din(idexe_reg_1_exe_din),
    .id_ret_addr(id_1_ret_addr), .exe_ret_addr(idexe_reg_1_exe_ret_addr), .stall(stall), .rst(rst),
    .clk(clk_out));
  HILO hilo_1 (
    .we(wb_1_wb_whilo_o), .in_2(wb_1_wb_hi_o), .in_3(wb_1_wb_lo_o), .clk(clk_out), .out_5(hilo_1_out_5),
    .out_6(hilo_1_out_6));
  Multiplexer #(.select(2), .width(32), .enable("false")) multiplexer_1 (
    .in0(hilo_1_out_5), .in1(mem_1_mem2exe_hi), .in2(wb_1_wb2exe_hi), .out(multiplexer_1_out),
    .sel(mem_1_mem2exe_whilo));  // open: in3
  Multiplexer #(.select(2), .width(32), .enable("false")) multiplexer_2 (
    .in0(hilo_1_out_6), .in1(mem_1_mem2exe_lo), .in2(wb_1_wb2exe_lo), .out(multiplexer_2_out),
    .sel(mem_1_mem2exe_whilo));  // open: in3
  exe exe_1 (
    .exe_mreg_i(idexe_reg_1_exe_mreg), .exe_whilo_i(idexe_reg_1_exe_whilo),
    .exe_wreg_i(idexe_reg_1_exe_wreg), .exe_alutype_i(idexe_reg_1_exe_alutype),
    .exe_aluop_i(idexe_reg_1_exe_aluop), .exe_wa_i(idexe_reg_1_exe_wa), .exe_src1_i(idexe_reg_1_exe_src1),
    .exe_src2_i(idexe_reg_1_exe_src2), .exe_din_i(idexe_reg_1_exe_din), .hi_i(multiplexer_1_out),
    .lo_i(multiplexer_2_out), .rst(rst), .exe_mreg_o(exe_1_exe_mreg_o), .exe_whilo_o(exe_1_exe_whilo_o),
    .exe_wreg_o(exe_1_exe_wreg_o), .exe_aluop_o(exe_1_exe_aluop_o), .exe_wa_o(exe_1_exe_wa_o),
    .exe_hi_o(exe_1_exe_hi_o), .exe_lo_o(exe_1_exe_lo_o), .exe_wd_o(exe_1_exe_wd_o),
    .exe_din_o(exe_1_exe_din_o), .exe2id_wreg(exe_1_exe2id_wreg), .exe2id_wa(exe_1_exe2id_wa),
    .exe2id_wd(exe_1_exe2id_wd), .exe_ret_addr(idexe_reg_1_exe_ret_addr), .clk(clk_out),
    .stallreq_exe(stallreq_exe), .exe2id_mreg(emreg));
  exemem_reg exemem_reg_1 (
    .exe_mreg(exe_1_exe_mreg_o), .exe_whilo(exe_1_exe_whilo_o), .exe_wreg(exe_1_exe_wreg_o),
    .exe_aluop(exe_1_exe_aluop_o), .exe_wa(exe_1_exe_wa_o), .exe_hi(exe_1_exe_hi_o), .exe_lo(exe_1_exe_lo_o),
    .exe_wd(exe_1_exe_wd_o), .exe_din(exe_1_exe_din_o), .mem_mreg(exemem_reg_1_mem_mreg),
    .mem_whilo(exemem_reg_1_mem_whilo), .mem_wreg(exemem_reg_1_mem_wreg), .mem_aluop(exemem_reg_1_mem_aluop),
    .mem_wa(exemem_reg_1_mem_wa), .mem_hi(exemem_reg_1_mem_hi), .mem_lo(exemem_reg_1_mem_lo),
    .mem_wd(exemem_reg_1_mem_wd), .mem_din(exemem_reg_1_mem_din), .rst(rst), .clk(clk_out), .stall(stall));
  mem mem_1 (
    .mem_mreg_i(exemem_reg_1_mem_mreg), .mem_whilo_i(exemem_reg_1_mem_whilo),
    .mem_wreg_i(exemem_reg_1_mem_wreg), .mem_aluop_i(exemem_reg_1_mem_aluop), .mem_wa_i(exemem_reg_1_mem_wa),
    .mem_hi_i(exemem_reg_1_mem_hi), .mem_lo_i(exemem_reg_1_mem_lo), .mem_wd_i(exemem_reg_1_mem_wd),
    .mem_din_i(exemem_reg_1_mem_din), .rst(rst), .mem_mreg_o(mem_1_mem_mreg_o),
    .mem_whilo_o(mem_1_mem_whilo_o), .mem_wreg_o(mem_1_mem_wreg_o), .mem_wa_o(mem_1_mem_wa_o),
    .mem_hi_o(mem_1_mem_hi_o), .mem_lo_o(mem_1_mem_lo_o), .mem_dreg_o(mem_1_mem_dreg_o), .dre(mem_1_dre),
    .dce(mem_1_dce), .daddr(mem_1_daddr), .we(mem_1_we), .din(mem_1_din), .mem2id_wa(mem_1_mem2id_wa),
    .mem2id_wreg(mem_1_mem2id_wreg), .mem2id_wd(mem_1_mem2id_wd), .mem2exe_whilo(mem_1_mem2exe_whilo[0]),
    .mem2exe_hi(mem_1_mem2exe_hi), .mem2exe_lo(mem_1_mem2exe_lo), .mem2id_mreg(mmreg));
  DM dm_1 (
    .daddr(mem_1_daddr), .we(mem_1_we), .dce(mem_1_dce), .din(mem_1_din), .dout(dm_1_dout), .clk(clk_out),
    .rst(rst));
  SCU scu_1 (.stallreq_id(stallreq_id), .stallreq_exe(stallreq_exe), .stall(stall));
  memwb_reg memwb_reg_1 (
    .mem_mreg(mem_1_mem_mreg_o), .mem_whilo(mem_1_mem_whilo_o), .mem_wreg(mem_1_mem_wreg_o),
    .mem_wa(mem_1_mem_wa_o), .mem_hi(mem_1_mem_hi_o), .mem_lo(mem_1_mem_lo_o), .mem_dreg(mem_1_mem_dreg_o),
    .mem_dre(mem_1_dre), .rst(rst), .clk(clk_out), .wb_mreg(memwb_reg_1_wb_mreg),
    .wb_whilo(memwb_reg_1_wb_whilo), .wb_wreg(memwb_reg_1_wb_wreg), .wb_wa(memwb_reg_1_wb_wa),
    .wb_hi(memwb_reg_1_wb_hi), .wb_lo(memwb_reg_1_wb_lo), .wb_dreg(memwb_reg_1_wb_dreg),
    .wb_dre(memwb_reg_1_wb_dre), .mem_dm(dm_1_dout), .wb_dm(memwb_reg_1_wb_dm));
  wb wb_1 (
    .wb_mreg_i(memwb_reg_1_wb_mreg), .wb_whilo_i(memwb_reg_1_wb_whilo), .wb_wreg_i(memwb_reg_1_wb_wreg),
    .wb_wa_i(memwb_reg_1_wb_wa), .wb_hi_i(memwb_reg_1_wb_hi), .wb_lo_i(memwb_reg_1_wb_lo),
    .wb_dreg_i(memwb_reg_1_wb_dreg), .dm(memwb_reg_1_wb_dm), .clk(clk_out), .wb_whilo_o(wb_1_wb_whilo_o),
    .wb_wreg_o(wb_1_wb_wreg_o), .wb_wa_o(wb_1_wb_wa_o), .wb_hi_o(wb_1_wb_hi_o), .wb_lo_o(wb_1_wb_lo_o),
    .wb_wd_o(wb_1_wb_wd_o), .wb_dre_i(memwb_reg_1_wb_dre), .wb2exe_whilo(mem_1_mem2exe_whilo[1]),
    .wb2exe_hi(wb_1_wb2exe_hi), .wb2exe_lo(wb_1_wb2exe_lo));
endmodule

module IM (
  input  [23:0] iaddr,
  input  ice,
  output [31:0] inst
);

  ROM #(.addrWidth(24), .dataWidth(32)) rom_1 (.addr(iaddr), .data(inst), .sel(ice));

  // Notes on the sheet:
  //   contents of rom_1 (hex, n*v repeats v):
  //   1010013c 11112134 1ac 1010134 10000234 1a002200 38c 6424
endmodule

module DM (
  input  [23:0] daddr,
  input  dce,
  input  [3:0] we,
  input  [31:0] din,
  input  clk,
  input  rst,
  output [31:0] dout
);

  wire not_1_out, not_2_out, not_3_out, not_4_out;

  not not_1 (not_1_out, rst);
  RAM #(.addrWidth(24), .bus("separate")) ram_1 (
    .addr(daddr), .din(din[7:0]), .data(dout[7:0]), .str(we[0]), .sel(dce), .clk(clk), .ld(1'b1),
    .clr(not_1_out));
  RAM #(.addrWidth(24), .bus("separate")) ram_2 (
    .addr(daddr), .din(din[15:8]), .data(dout[15:8]), .str(we[1]), .sel(dce), .clk(clk), .ld(1'b1),
    .clr(not_2_out));
  not not_2 (not_2_out, rst);
  RAM #(.addrWidth(24), .bus("separate")) ram_3 (
    .addr(daddr), .din(din[23:16]), .data(dout[23:16]), .str(we[2]), .sel(dce), .clk(clk), .ld(1'b1),
    .clr(not_3_out));
  not not_3 (not_3_out, rst);
  not not_4 (not_4_out, rst);
  RAM #(.addrWidth(24), .bus("separate")) ram_4 (
    .addr(daddr), .din(din[31:24]), .data(dout[31:24]), .str(we[3]), .sel(dce), .clk(clk), .ld(1'b1),
    .clr(not_4_out));
endmodule

module RegFile (
  input  clk,
  input  [31:0] wd,
  input  we,
  input  [4:0] ra1,
  input  [4:0] wa,
  input  re1,
  input  [4:0] ra2,
  input  re1_2,
  output [31:0] rd1,
  output [31:0] rd2
);

  wire and_1_out, and_2_out, comparator_1_eq, comparator_2_eq, demultiplexer_1_out0, demultiplexer_1_out1,
       demultiplexer_1_out2, demultiplexer_1_out3, demultiplexer_1_out4, demultiplexer_1_out5,
       demultiplexer_1_out6, demultiplexer_1_out7, demultiplexer_1_out8, demultiplexer_1_out9,
       demultiplexer_1_out10, demultiplexer_1_out11, demultiplexer_1_out12, demultiplexer_1_out13,
       demultiplexer_1_out14, demultiplexer_1_out15, demultiplexer_1_out16, demultiplexer_1_out17,
       demultiplexer_1_out18, demultiplexer_1_out19, demultiplexer_1_out20, demultiplexer_1_out21,
       demultiplexer_1_out22, demultiplexer_1_out23, demultiplexer_1_out24, demultiplexer_1_out25,
       demultiplexer_1_out26, demultiplexer_1_out27, demultiplexer_1_out28, demultiplexer_1_out29,
       demultiplexer_1_out30, demultiplexer_1_out31;
  wire [31:0] multiplexer_1_out, multiplexer_2_out, register_1_q, register_2_q, register_3_q, register_4_q,
       register_5_q, register_6_q, register_7_q, register_8_q, register_9_q, register_10_q, register_11_q,
       register_12_q, register_13_q, register_14_q, register_15_q, register_16_q, register_17_q,
       register_18_q, register_19_q, register_20_q, register_21_q, register_22_q, register_23_q,
       register_24_q, register_25_q, register_26_q, register_27_q, register_28_q, register_29_q,
       register_30_q, register_31_q, register_32_q;

  Demultiplexer #(.select(5), .enable("false")) demultiplexer_1 (
    .out0(demultiplexer_1_out0), .out1(demultiplexer_1_out1), .out2(demultiplexer_1_out2),
    .out3(demultiplexer_1_out3), .out4(demultiplexer_1_out4), .out5(demultiplexer_1_out5),
    .out6(demultiplexer_1_out6), .out7(demultiplexer_1_out7), .out8(demultiplexer_1_out8),
    .out9(demultiplexer_1_out9), .out10(demultiplexer_1_out10), .out11(demultiplexer_1_out11),
    .out12(demultiplexer_1_out12), .out13(demultiplexer_1_out13), .out14(demultiplexer_1_out14),
    .out15(demultiplexer_1_out15), .out16(demultiplexer_1_out16), .out17(demultiplexer_1_out17),
    .out18(demultiplexer_1_out18), .out19(demultiplexer_1_out19), .out20(demultiplexer_1_out20),
    .out21(demultiplexer_1_out21), .out22(demultiplexer_1_out22), .out23(demultiplexer_1_out23),
    .out24(demultiplexer_1_out24), .out25(demultiplexer_1_out25), .out26(demultiplexer_1_out26),
    .out27(demultiplexer_1_out27), .out28(demultiplexer_1_out28), .out29(demultiplexer_1_out29),
    .out30(demultiplexer_1_out30), .out31(demultiplexer_1_out31), .in(we), .sel(wa));
  Register #(.width(32)) register_1 (.D(wd), .en(demultiplexer_1_out0), .Q(register_1_q), .clk(clk));  // open: clr
  Register #(.width(32)) register_2 (.D(wd), .en(demultiplexer_1_out1), .Q(register_2_q), .clk(clk));  // open: clr
  Register #(.width(32)) register_3 (.D(wd), .en(demultiplexer_1_out2), .Q(register_3_q), .clk(clk));  // open: clr
  Register #(.width(32)) register_4 (.D(wd), .en(demultiplexer_1_out3), .Q(register_4_q), .clk(clk));  // open: clr
  Register #(.width(32)) register_5 (.D(wd), .en(demultiplexer_1_out4), .Q(register_5_q), .clk(clk));  // open: clr
  Register #(.width(32)) register_6 (.D(wd), .en(demultiplexer_1_out5), .Q(register_6_q), .clk(clk));  // open: clr
  Register #(.width(32)) register_7 (.D(wd), .en(demultiplexer_1_out6), .Q(register_7_q), .clk(clk));  // open: clr
  Register #(.width(32)) register_8 (.D(wd), .en(demultiplexer_1_out7), .Q(register_8_q), .clk(clk));  // open: clr
  Register #(.width(32)) register_9 (.D(wd), .en(demultiplexer_1_out8), .Q(register_9_q), .clk(clk));  // open: clr
  Register #(.width(32)) register_10 (.D(wd), .en(demultiplexer_1_out9), .Q(register_10_q), .clk(clk));  // open: clr
  Register #(.width(32)) register_11 (.D(wd), .en(demultiplexer_1_out10), .Q(register_11_q), .clk(clk));  // open: clr
  Register #(.width(32)) register_12 (.D(wd), .en(demultiplexer_1_out11), .Q(register_12_q), .clk(clk));  // open: clr
  Register #(.width(32)) register_13 (.D(wd), .en(demultiplexer_1_out12), .Q(register_13_q), .clk(clk));  // open: clr
  Register #(.width(32)) register_14 (.D(wd), .en(demultiplexer_1_out13), .Q(register_14_q), .clk(clk));  // open: clr
  Register #(.width(32)) register_15 (.D(wd), .en(demultiplexer_1_out14), .Q(register_15_q), .clk(clk));  // open: clr
  Register #(.width(32)) register_16 (.D(wd), .en(demultiplexer_1_out15), .Q(register_16_q), .clk(clk));  // open: clr
  Register #(.width(32)) register_17 (.D(wd), .en(demultiplexer_1_out16), .Q(register_17_q), .clk(clk));  // open: clr
  Register #(.width(32)) register_18 (.D(wd), .en(demultiplexer_1_out17), .Q(register_18_q), .clk(clk));  // open: clr
  Register #(.width(32)) register_19 (.D(wd), .en(demultiplexer_1_out18), .Q(register_19_q), .clk(clk));  // open: clr
  Register #(.width(32)) register_20 (.D(wd), .en(demultiplexer_1_out19), .Q(register_20_q), .clk(clk));  // open: clr
  Register #(.width(32)) register_21 (.D(wd), .en(demultiplexer_1_out20), .Q(register_21_q), .clk(clk));  // open: clr
  Register #(.width(32)) register_22 (.D(wd), .en(demultiplexer_1_out21), .Q(register_22_q), .clk(clk));  // open: clr
  Register #(.width(32)) register_23 (.D(wd), .en(demultiplexer_1_out22), .Q(register_23_q), .clk(clk));  // open: clr
  Register #(.width(32)) register_24 (.D(wd), .en(demultiplexer_1_out23), .Q(register_24_q), .clk(clk));  // open: clr
  Register #(.width(32)) register_25 (.D(wd), .en(demultiplexer_1_out24), .Q(register_25_q), .clk(clk));  // open: clr
  Register #(.width(32)) register_26 (.D(wd), .en(demultiplexer_1_out25), .Q(register_26_q), .clk(clk));  // open: clr
  Register #(.width(32)) register_27 (.D(wd), .en(demultiplexer_1_out26), .Q(register_27_q), .clk(clk));  // open: clr
  Register #(.width(32)) register_28 (.D(wd), .en(demultiplexer_1_out27), .Q(register_28_q), .clk(clk));  // open: clr
  Register #(.width(32)) register_29 (.D(wd), .en(demultiplexer_1_out28), .Q(register_29_q), .clk(clk));  // open: clr
  Register #(.width(32)) register_30 (.D(wd), .en(demultiplexer_1_out29), .Q(register_30_q), .clk(clk));  // open: clr
  Register #(.width(32)) register_31 (.D(wd), .en(demultiplexer_1_out30), .Q(register_31_q), .clk(clk));  // open: clr
  Register #(.width(32)) register_32 (.D(wd), .en(demultiplexer_1_out31), .Q(register_32_q), .clk(clk));  // open: clr
  Multiplexer #(.select(5), .width(32)) multiplexer_1 (
    .in0(register_1_q), .in1(register_2_q), .in2(register_3_q), .in3(register_4_q), .in4(register_5_q),
    .in5(register_6_q), .in6(register_7_q), .in7(register_8_q), .in8(register_9_q), .in9(register_10_q),
    .in10(register_11_q), .in11(register_12_q), .in12(register_13_q), .in13(register_14_q),
    .in14(register_15_q), .in15(register_16_q), .in16(register_17_q), .in17(register_18_q),
    .in18(register_19_q), .in19(register_20_q), .in20(register_21_q), .in21(register_22_q),
    .in22(register_23_q), .in23(register_24_q), .in24(register_25_q), .in25(register_26_q),
    .in26(register_27_q), .in27(register_28_q), .in28(register_29_q), .in29(register_30_q),
    .in30(register_31_q), .in31(register_32_q), .out(multiplexer_1_out), .sel(ra1), .en(re1));
  Multiplexer #(.select(5), .width(32)) multiplexer_2 (
    .in0(register_1_q), .in1(register_2_q), .in2(register_3_q), .in3(register_4_q), .in4(register_5_q),
    .in5(register_6_q), .in6(register_7_q), .in7(register_8_q), .in8(register_9_q), .in9(register_10_q),
    .in10(register_11_q), .in11(register_12_q), .in12(register_13_q), .in13(register_14_q),
    .in14(register_15_q), .in15(register_16_q), .in16(register_17_q), .in17(register_18_q),
    .in18(register_19_q), .in19(register_20_q), .in20(register_21_q), .in21(register_22_q),
    .in22(register_23_q), .in23(register_24_q), .in24(register_25_q), .in25(register_26_q),
    .in26(register_27_q), .in27(register_28_q), .in28(register_29_q), .in29(register_30_q),
    .in30(register_31_q), .in31(register_32_q), .out(multiplexer_2_out), .sel(ra2), .en(re1_2));
  Comparator #(.width(5), .mode("unsigned")) comparator_1 (.a(ra1), .b(wa), .eq(comparator_1_eq));  // open: gt, lt
  Comparator #(.width(5), .mode("unsigned")) comparator_2 (.a(ra2), .b(wa), .eq(comparator_2_eq));  // open: gt, lt
  and and_1 (and_1_out, comparator_1_eq, we);
  and and_2 (and_2_out, comparator_2_eq, we);
  Multiplexer #(.width(32)) multiplexer_3 (.in0(multiplexer_1_out), .in1(wd), .out(rd1), .sel(and_1_out), .en(re1));
  Multiplexer #(.width(32)) multiplexer_4 (.in0(multiplexer_2_out), .in1(wd), .out(rd2), .sel(and_2_out), .en(re1_2));
endmodule

module \if  (
  input  [31:0] addr3,
  input  [31:0] addr1,
  input  [1:0] jtsel,
  input  [31:0] addr2,
  input  [3:0] stall,
  input  rst,
  input  clk,
  output [31:0] pc,
  output [23:0] iaddr,
  output ice
);

  wire and_1_out, not_1_out, not_2_out, not_3_out, not_4_out;
  wire [31:0] adder_1_out, multiplexer_1_out;

  not not_1 (not_1_out, stall[0]);
  Register #(.width(32)) u_PC (
    .D(multiplexer_1_out), .en(not_1_out), .Q({pc[31:26], iaddr, pc[1:0]}), .clk(clk), .clr(not_2_out));
  not not_2 (not_2_out, rst);
  Multiplexer #(.select(2), .width(32), .enable("false")) multiplexer_1 (
    .in0(adder_1_out), .in1(addr3), .in2(addr1), .in3(addr2), .out(multiplexer_1_out), .sel(jtsel));
  Adder #(.width(32)) adder_1 (.a(32'h4), .b({pc[31:26], iaddr, pc[1:0]}), .out(adder_1_out));  // open: cin, cout
  not not_3 (not_3_out, stall[1]);
  and and_1 (and_1_out, stall[0], not_3_out);
  not not_4 (not_4_out, and_1_out);
  and and_2 (ice, not_4_out, rst);

  assign pc[25:2] = iaddr;
endmodule

module ifid_reg (
  input  [31:0] if_pc,
  input  [31:0] if_inst,
  input  [3:0] stall,
  input  rst,
  input  clk,
  output [31:0] id_pc,
  output [31:0] id_inst
);

  wire and_1_out, and_2_out, not_1_out, not_2_out;
  wire [31:0] multiplexer_1_out, multiplexer_2_out;

  not not_1 (not_1_out, stall[2]);
  and and_1 (and_1_out, stall[1], not_1_out);
  Multiplexer #(.width(32), .enable("false")) multiplexer_1 (
    .in0(if_pc), .in1({32{1'b0}}), .out(multiplexer_1_out), .sel(and_1_out));
  Multiplexer #(.width(32), .enable("false")) multiplexer_2 (
    .in0(if_inst), .in1({32{1'b0}}), .out(multiplexer_2_out), .sel(and_1_out));
  and and_2 (and_2_out, not_1_out, rst);
  not not_2 (not_2_out, rst);
  Register #(.width(32)) pc (.D(multiplexer_1_out), .en(and_2_out), .Q(id_pc), .clk(clk), .clr(not_2_out));
  Register #(.width(32)) register_1 (.D(multiplexer_2_out), .en(and_2_out), .Q(id_inst), .clk(clk), .clr(not_2_out));
endmodule

module id (
  input  [31:0] id_pc_i,
  input  [4:0] exe2id_wa,
  input  [4:0] mem2id_wa,
  input  exe2id_wreg,
  input  mem2id_wreg,
  input  [31:0] rd1,
  input  [31:0] id_inst_i,
  input  [31:0] rd2,
  input  [31:0] exe2id_wd,
  input  [31:0] mem2id_wd,
  input  rst,
  input  exe2id_mreg,
  input  mem2id_mreg,
  output [31:0] ret_addr,
  output [31:0] addr3,
  output [31:0] addr1,
  output [31:0] addr2,
  output [1:0] jtsel,
  output id_mreg_o,
  output id_whilo_o,
  output id_wreg_o,
  output [2:0] id_alutype_o,
  output [7:0] id_aluop_o,
  output rreg1,
  output rreg2,
  output [4:0] id_wa_o,
  output [31:0] id_src1_o,
  output [4:0] ra1,
  output [4:0] ra2,
  output [31:0] id_src2_o,
  output [31:0] id_din_o,
  output stallreq_id
);

  wire and_1_out, and_2_out, and_3_out, and_4_out, and_5_out, and_6_out, comparator_1_eq, comparator_2_eq,
       comparator_3_eq, comparator_4_eq, comparator_5_eq, dcu_1_immsel, dcu_1_jal, dcu_1_rtsel, dcu_1_sext,
       dcu_1_shift, dcu_1_upper, or_1_out, or_2_out;
  wire [1:0] dcu_1_fwrd1, dcu_1_fwrd2;
  wire [4:0] multiplexer_1_out;
  wire [31:0] bit_extender_1_out, bit_extender_2_out, bit_extender_3_out, multiplexer_2_out,
       multiplexer_3_out, multiplexer_4_out, shifter_1_out;

  Adder #(.width(32)) adder_1 (.a(32'h8), .b(id_pc_i), .out(ret_addr));  // open: cin, cout
  id_addr1 id_addr1_1 (
    .instr_index({id_inst_i[1:0], id_inst_i[15:8], id_inst_i[23:16], id_inst_i[31:24]}), .pc(id_pc_i),
    .addr1(addr1));
  id_addr2 id_addr2_1 (.pc(id_pc_i), .imm({id_inst_i[23:16], id_inst_i[31:24]}), .addr2(addr2));
  assign bit_extender_1_out = {{27{1'b0}}, {id_inst_i[18:16], id_inst_i[31:30]}};  // Bit_Extender bit_extender_1
  assign bit_extender_2_out = {{16{1'b0}}, {id_inst_i[23:16], id_inst_i[31:24]}};  // Bit_Extender bit_extender_2
  assign bit_extender_3_out = {{16{id_inst_i[23]}}, {id_inst_i[23:16], id_inst_i[31:24]}};  // Bit_Extender bit_extender_3
  Multiplexer #(.width(5), .enable("false")) multiplexer_1 (
    .in0(id_inst_i[23:19]), .in1(id_inst_i[12:8]), .out(multiplexer_1_out), .sel(dcu_1_rtsel));
  Multiplexer #(.width(32), .enable("false")) multiplexer_2 (
    .in0(bit_extender_2_out), .in1(bit_extender_3_out), .out(multiplexer_2_out), .sel(dcu_1_sext));
  Shifter #(.width(32)) shifter_1 (.in(bit_extender_2_out), .\dist (5'b10000), .out(shifter_1_out));
  DCU dcu_1 (
    .op(id_inst_i[7:2]), .func(id_inst_i[29:24]), .aluop(id_aluop_o), .alutype(id_alutype_o), .rreg1(rreg1),
    .rreg2(rreg2), .wreg(id_wreg_o), .whilo(id_whilo_o), .immsel(dcu_1_immsel), .rtsel(dcu_1_rtsel),
    .sext(dcu_1_sext), .upper(dcu_1_upper), .mreg(id_mreg_o), .shift(dcu_1_shift),
    .rs({id_inst_i[1:0], id_inst_i[15:13]}), .rt(id_inst_i[12:8]), .exe2id_wa(exe2id_wa),
    .mem2id_wa(mem2id_wa), .exe2id_wreg(exe2id_wreg), .mem2id_wreg(mem2id_wreg), .fwrd1(dcu_1_fwrd1),
    .fwrd2(dcu_1_fwrd2), .equ(comparator_5_eq), .jal(dcu_1_jal), .jtsel(jtsel));
  Comparator #(.width(5), .mode("unsigned")) comparator_1 (
    .a(exe2id_wa), .b({id_inst_i[1:0], id_inst_i[15:13]}), .eq(comparator_1_eq));  // open: gt, lt
  Comparator #(.width(5), .mode("unsigned")) comparator_2 (
    .a(exe2id_wa), .b(id_inst_i[12:8]), .eq(comparator_2_eq));  // open: gt, lt
  Comparator #(.width(5), .mode("unsigned")) comparator_3 (
    .a(mem2id_wa), .b({id_inst_i[1:0], id_inst_i[15:13]}), .eq(comparator_3_eq));  // open: gt, lt
  Comparator #(.width(5), .mode("unsigned")) comparator_4 (
    .a(mem2id_wa), .b(id_inst_i[12:8]), .eq(comparator_4_eq));  // open: gt, lt
  Multiplexer #(.width(32), .enable("false")) multiplexer_3 (
    .in0(multiplexer_2_out), .in1(shifter_1_out), .out(multiplexer_3_out), .sel(dcu_1_upper));
  Multiplexer #(.select(2), .width(32), .enable("false")) multiplexer_4 (
    .in0(rd1), .in1(exe2id_wd), .in2(mem2id_wd), .in3(exe2id_wd), .out(multiplexer_4_out), .sel(dcu_1_fwrd1));
  Multiplexer #(.select(2), .width(32), .enable("false")) multiplexer_5 (
    .in0(rd2), .in1(exe2id_wd), .in2(mem2id_wd), .in3(exe2id_wd), .out(id_din_o), .sel(dcu_1_fwrd2));
  and and_1 (and_1_out, exe2id_wreg, rreg1, comparator_1_eq);
  and and_2 (and_2_out, exe2id_wreg, rreg2, comparator_2_eq);
  and and_3 (and_3_out, mem2id_wreg, comparator_3_eq, rreg1);
  and and_4 (and_4_out, mem2id_wreg, comparator_4_eq, rreg2);
  Multiplexer #(.width(5), .enable("false")) multiplexer_6 (
    .in0(multiplexer_1_out), .in1({5{1'b1}}), .out(id_wa_o), .sel(dcu_1_jal));
  or or_1 (or_1_out, and_1_out, and_2_out);
  or or_2 (or_2_out, and_3_out, and_4_out);
  Multiplexer #(.width(32), .enable("false")) multiplexer_7 (
    .in0(multiplexer_4_out), .in1(bit_extender_1_out), .out(addr3), .sel(dcu_1_shift));
  Multiplexer #(.width(32), .enable("false")) multiplexer_8 (
    .in0(id_din_o), .in1(multiplexer_3_out), .out(id_src2_o), .sel(dcu_1_immsel));
  and and_5 (and_5_out, or_1_out, exe2id_mreg);
  and and_6 (and_6_out, mem2id_mreg, or_2_out);
  Comparator #(.width(32), .mode("unsigned")) comparator_5 (
    .a(addr3), .b(id_src2_o), .eq(comparator_5_eq));  // open: gt, lt
  or or_3 (stallreq_id, and_5_out, and_6_out);

  assign id_src1_o = addr3;
  assign ra1 = {id_inst_i[1:0], id_inst_i[15:13]};
  assign ra2 = id_inst_i[12:8];

  // Notes on the sheet:
  //   instr_index
  //   op
  //   func
  //   rd
  //   rs
  //   rt
  //   rt
  //   sa
  //   imm
endmodule

module id_addr1 (
  input  [25:0] instr_index,
  input  [31:0] pc,
  output [31:0] addr1
);

  wire [27:0] adder_1_out;

  Adder #(.width(32)) adder_1 (.a(32'h4), .b(pc), .out({addr1[31:28], adder_1_out}));  // open: cin, cout

  assign addr1[27:0] = {instr_index, 2'b00};
endmodule

module id_addr2 (
  input  [31:0] pc,
  input  [15:0] imm,
  output [31:0] addr2
);

  wire [31:0] adder_1_out, bit_extender_1_out;

  Adder #(.width(32)) adder_1 (.a(32'h4), .b(pc), .out(adder_1_out));  // open: cin, cout
  assign bit_extender_1_out = {{14{imm[15]}}, {imm, 2'b00}};  // Bit_Extender bit_extender_1
  Adder #(.width(32)) adder_2 (.a(adder_1_out), .b(bit_extender_1_out), .out(addr2));  // open: cin, cout
endmodule

module idexe_reg (
  input  id_mreg,
  input  id_whilo,
  input  id_wreg,
  input  [2:0] id_alutype,
  input  [7:0] id_aluop,
  input  [4:0] id_wa,
  input  [31:0] id_src1,
  input  [31:0] id_src2,
  input  [31:0] id_din,
  input  [31:0] id_ret_addr,
  input  [3:0] stall,
  input  rst,
  input  clk,
  output exe_mreg,
  output exe_whilo,
  output exe_wreg,
  output [2:0] exe_alutype,
  output [7:0] exe_aluop,
  output [4:0] exe_wa,
  output [31:0] exe_src1,
  output [31:0] exe_src2,
  output [31:0] exe_din,
  output [31:0] exe_ret_addr
);

  wire and_1_out, and_2_out, multiplexer_1_out, multiplexer_2_out, multiplexer_3_out, not_1_out, not_2_out;
  wire [2:0] multiplexer_4_out;
  wire [4:0] multiplexer_6_out;
  wire [7:0] multiplexer_5_out;
  wire [31:0] multiplexer_7_out, multiplexer_8_out, multiplexer_9_out, multiplexer_10_out;

  not not_1 (not_1_out, stall[3]);
  and and_1 (and_1_out, stall[2], not_1_out);
  Multiplexer #(.enable("false")) multiplexer_1 (.in0(id_mreg), .in1(1'b0), .out(multiplexer_1_out), .sel(and_1_out));
  Multiplexer #(.enable("false")) multiplexer_2 (.in0(id_whilo), .in1(1'b0), .out(multiplexer_2_out), .sel(and_1_out));
  Multiplexer #(.enable("false")) multiplexer_3 (.in0(id_wreg), .in1(1'b0), .out(multiplexer_3_out), .sel(and_1_out));
  Multiplexer #(.width(3), .enable("false")) multiplexer_4 (
    .in0(id_alutype), .in1(3'b000), .out(multiplexer_4_out), .sel(and_1_out));
  Multiplexer #(.width(8), .enable("false")) multiplexer_5 (
    .in0(id_aluop), .in1({8{1'b0}}), .out(multiplexer_5_out), .sel(and_1_out));
  Multiplexer #(.width(5), .enable("false")) multiplexer_6 (
    .in0(id_wa), .in1({5{1'b0}}), .out(multiplexer_6_out), .sel(and_1_out));
  Multiplexer #(.width(32), .enable("false")) multiplexer_7 (
    .in0(id_src1), .in1({32{1'b0}}), .out(multiplexer_7_out), .sel(and_1_out));
  Multiplexer #(.width(32), .enable("false")) multiplexer_8 (
    .in0(id_src2), .in1({32{1'b0}}), .out(multiplexer_8_out), .sel(and_1_out));
  Multiplexer #(.width(32), .enable("false")) multiplexer_9 (
    .in0(id_din), .in1({32{1'b0}}), .out(multiplexer_9_out), .sel(and_1_out));
  Multiplexer #(.width(32), .enable("false")) multiplexer_10 (
    .in0(id_ret_addr), .in1({32{1'b0}}), .out(multiplexer_10_out), .sel(and_1_out));
  and and_2 (and_2_out, not_1_out, rst);
  not not_2 (not_2_out, rst);
  Register #(.width(1)) register_1 (.D(multiplexer_1_out), .en(and_2_out), .Q(exe_mreg), .clk(clk), .clr(not_2_out));
  Register #(.width(1)) register_2 (.D(multiplexer_2_out), .en(and_2_out), .Q(exe_whilo), .clk(clk), .clr(not_2_out));
  Register #(.width(1)) register_3 (.D(multiplexer_3_out), .en(and_2_out), .Q(exe_wreg), .clk(clk), .clr(not_2_out));
  Register #(.width(3)) register_4 (.D(multiplexer_4_out), .en(and_2_out), .Q(exe_alutype), .clk(clk), .clr(not_2_out));
  Register register_5 (.D(multiplexer_5_out), .en(and_2_out), .Q(exe_aluop), .clk(clk), .clr(not_2_out));
  Register #(.width(5)) register_6 (.D(multiplexer_6_out), .en(and_2_out), .Q(exe_wa), .clk(clk), .clr(not_2_out));
  Register #(.width(32)) register_7 (.D(multiplexer_7_out), .en(and_2_out), .Q(exe_src1), .clk(clk), .clr(not_2_out));
  Register #(.width(32)) register_8 (.D(multiplexer_8_out), .en(and_2_out), .Q(exe_src2), .clk(clk), .clr(not_2_out));
  Register #(.width(32)) register_9 (.D(multiplexer_9_out), .en(and_2_out), .Q(exe_din), .clk(clk), .clr(not_2_out));
  Register #(.width(32)) register_10 (
    .D(multiplexer_10_out), .en(and_2_out), .Q(exe_ret_addr), .clk(clk), .clr(not_2_out));
endmodule

module exe (
  input  exe_mreg_i,
  input  exe_whilo_i,
  input  exe_wreg_i,
  input  [2:0] exe_alutype_i,
  input  [7:0] exe_aluop_i,
  input  [4:0] exe_wa_i,
  input  [31:0] exe_src1_i,
  input  [31:0] exe_src2_i,
  input  [31:0] exe_din_i,
  input  [31:0] hi_i,
  input  [31:0] lo_i,
  input  [31:0] exe_ret_addr,
  input  clk,
  input  rst,
  output stallreq_exe,
  output [4:0] exe2id_wa,
  output exe2id_mreg,
  output exe2id_wreg,
  output exe_mreg_o,
  output exe_whilo_o,
  output exe_wreg_o,
  output [7:0] exe_aluop_o,
  output [4:0] exe_wa_o,
  output [31:0] exe_hi_o,
  output [31:0] exe_lo_o,
  output [31:0] exe_wd_o,
  output [31:0] exe_din_o,
  output [31:0] exe2id_wd
);

  wire comparator_1_eq, comparator_2_eq, priority_encoder_1_out;
  wire [31:0] alu_1_arithres, alu_1_divres_hi, alu_1_divres_lo, alu_1_logicres, alu_1_mulres_hi,
       alu_1_mulres_lo, alu_1_shiftres, equalmux_1_out_4, equalmux_2_out_4, or_1_out;

  Comparator comparator_1 (.a(exe_aluop_i), .b(8'h14), .eq(comparator_1_eq));  // open: gt, lt
  Comparator comparator_2 (.a(exe_aluop_i), .b(8'h16), .eq(comparator_2_eq));  // open: gt, lt
  ALU alu_1 (
    .aluop(exe_aluop_i), .src1(exe_src1_i), .src2(exe_src2_i), .logicres(alu_1_logicres),
    .arithres(alu_1_arithres), .shiftres(alu_1_shiftres), .mulres_lo(alu_1_mulres_lo),
    .mulres_hi(alu_1_mulres_hi), .clk(clk), .divres_lo(alu_1_divres_lo), .divres_hi(alu_1_divres_hi),
    .stallreq_exe(stallreq_exe));
  EqualMux equalmux_1 (.src(hi_i), .en1(exe_aluop_i), .en2(8'hc), .out_4(equalmux_1_out_4));
  EqualMux equalmux_2 (.src(lo_i), .en1(exe_aluop_i), .en2(8'hd), .out_4(equalmux_2_out_4));
  Priority_Encoder #(.select(1)) priority_encoder_1 (
    .in0(comparator_1_eq), .in1(comparator_2_eq), .out(priority_encoder_1_out));  // open: gs, en_out, en_in
  assign or_1_out = equalmux_1_out_4 | equalmux_2_out_4;  // OR_Gate or_1, 32 bits wide
  Multiplexer #(.select(3), .width(32), .enable("false")) multiplexer_1 (
    .in1(alu_1_arithres), .in2(alu_1_logicres), .in3(or_1_out), .in4(alu_1_shiftres), .in5(exe_ret_addr),
    .out(exe2id_wd), .sel(exe_alutype_i));  // open: in0, in6, in7
  Multiplexer #(.width(32), .enable("false")) multiplexer_2 (
    .in0(alu_1_mulres_hi), .in1(alu_1_divres_hi), .out(exe_hi_o), .sel(priority_encoder_1_out));
  Multiplexer #(.width(32), .enable("false")) multiplexer_3 (
    .in0(alu_1_mulres_lo), .in1(alu_1_divres_lo), .out(exe_lo_o), .sel(priority_encoder_1_out));

  assign exe2id_mreg = exe_mreg_i;
  assign exe2id_wa = exe_wa_i;
  assign exe2id_wreg = exe_wreg_i;
  assign exe_aluop_o = exe_aluop_i;
  assign exe_din_o = exe_din_i;
  assign exe_mreg_o = exe_mreg_i;
  assign exe_wa_o = exe_wa_i;
  assign exe_wd_o = exe2id_wd;
  assign exe_whilo_o = exe_whilo_i;
  assign exe_wreg_o = exe_wreg_i;
endmodule

module exemem_reg (
  input  exe_mreg,
  input  exe_whilo,
  input  exe_wreg,
  input  [7:0] exe_aluop,
  input  [4:0] exe_wa,
  input  [31:0] exe_hi,
  input  [31:0] exe_lo,
  input  [31:0] exe_wd,
  input  [31:0] exe_din,
  input  [3:0] stall,
  input  rst,
  input  clk,
  output mem_mreg,
  output mem_whilo,
  output mem_wreg,
  output [7:0] mem_aluop,
  output [4:0] mem_wa,
  output [31:0] mem_hi,
  output [31:0] mem_lo,
  output [31:0] mem_wd,
  output [31:0] mem_din
);

  wire multiplexer_1_out, multiplexer_2_out, multiplexer_3_out, not_1_out;
  wire [4:0] multiplexer_5_out;
  wire [7:0] multiplexer_4_out;
  wire [31:0] multiplexer_6_out, multiplexer_7_out, multiplexer_8_out, multiplexer_9_out;

  Multiplexer #(.enable("false")) multiplexer_1 (.in0(exe_mreg), .in1(1'b0), .out(multiplexer_1_out), .sel(stall[3]));
  Multiplexer #(.enable("false")) multiplexer_2 (.in0(exe_whilo), .in1(1'b0), .out(multiplexer_2_out), .sel(stall[3]));
  Multiplexer #(.enable("false")) multiplexer_3 (.in0(exe_wreg), .in1(1'b0), .out(multiplexer_3_out), .sel(stall[3]));
  Multiplexer #(.width(8), .enable("false")) multiplexer_4 (
    .in0(exe_aluop), .in1({8{1'b0}}), .out(multiplexer_4_out), .sel(stall[3]));
  Multiplexer #(.width(5), .enable("false")) multiplexer_5 (
    .in0(exe_wa), .in1({5{1'b0}}), .out(multiplexer_5_out), .sel(stall[3]));
  Multiplexer #(.width(32), .enable("false")) multiplexer_6 (
    .in0(exe_hi), .in1({32{1'b0}}), .out(multiplexer_6_out), .sel(stall[3]));
  Multiplexer #(.width(32), .enable("false")) multiplexer_7 (
    .in0(exe_lo), .in1({32{1'b0}}), .out(multiplexer_7_out), .sel(stall[3]));
  Multiplexer #(.width(32), .enable("false")) multiplexer_8 (
    .in0(exe_wd), .in1({32{1'b0}}), .out(multiplexer_8_out), .sel(stall[3]));
  Multiplexer #(.width(32), .enable("false")) multiplexer_9 (
    .in0(exe_din), .in1({32{1'b0}}), .out(multiplexer_9_out), .sel(stall[3]));
  not not_1 (not_1_out, rst);
  Register #(.width(1)) register_1 (.D(multiplexer_1_out), .en(rst), .Q(mem_mreg), .clk(clk), .clr(not_1_out));
  Register #(.width(1)) register_2 (.D(multiplexer_2_out), .en(rst), .Q(mem_whilo), .clk(clk), .clr(not_1_out));
  Register #(.width(1)) register_3 (.D(multiplexer_3_out), .en(rst), .Q(mem_wreg), .clk(clk), .clr(not_1_out));
  Register register_4 (.D(multiplexer_4_out), .en(rst), .Q(mem_aluop), .clk(clk), .clr(not_1_out));
  Register #(.width(5)) register_5 (.D(multiplexer_5_out), .en(rst), .Q(mem_wa), .clk(clk), .clr(not_1_out));
  Register #(.width(32)) register_6 (.D(multiplexer_6_out), .en(rst), .Q(mem_hi), .clk(clk), .clr(not_1_out));
  Register #(.width(32)) register_7 (.D(multiplexer_7_out), .en(rst), .Q(mem_lo), .clk(clk), .clr(not_1_out));
  Register #(.width(32)) register_8 (.D(multiplexer_8_out), .en(rst), .Q(mem_wd), .clk(clk), .clr(not_1_out));
  Register #(.width(32)) register_9 (.D(multiplexer_9_out), .en(rst), .Q(mem_din), .clk(clk), .clr(not_1_out));
endmodule

module mem (
  input  mem_mreg_i,
  input  mem_whilo_i,
  input  mem_wreg_i,
  input  [7:0] mem_aluop_i,
  input  [4:0] mem_wa_i,
  input  [31:0] mem_hi_i,
  input  [31:0] mem_lo_i,
  input  [31:0] mem_wd_i,
  input  [31:0] mem_din_i,
  input  rst,
  output [4:0] mem2id_wa,
  output mem2id_mreg,
  output mem2id_wreg,
  output mem_mreg_o,
  output mem_whilo_o,
  output mem_wreg_o,
  output mem2exe_whilo,
  output [4:0] mem_wa_o,
  output [31:0] mem_hi_o,
  output [31:0] mem_lo_o,
  output [31:0] mem_dreg_o,
  output [31:0] mem2exe_hi,
  output [31:0] mem2exe_lo,
  output [3:0] dre,
  output dce,
  output [23:0] daddr,
  output [3:0] we,
  output [31:0] din,
  output [31:0] mem2id_wd
);

  MCU mcu_1 (.maddr(mem_wd_i), .aluop(mem_aluop_i), .dre(dre), .we(we), .dce(dce));

  assign daddr = mem_wd_i[25:2];
  assign din = {mem_din_i[7:0], mem_din_i[15:8], mem_din_i[23:16], mem_din_i[31:24]};
  assign mem2exe_hi = mem_hi_i;
  assign mem2exe_lo = mem_lo_i;
  assign mem2exe_whilo = mem_whilo_i;
  assign mem2id_mreg = mem_mreg_i;
  assign mem2id_wa = mem_wa_i;
  assign mem2id_wd = mem_wd_i;
  assign mem2id_wreg = mem_wreg_i;
  assign mem_dreg_o = mem_wd_i;
  assign mem_hi_o = mem_hi_i;
  assign mem_lo_o = mem_lo_i;
  assign mem_mreg_o = mem_mreg_i;
  assign mem_wa_o = mem_wa_i;
  assign mem_whilo_o = mem_whilo_i;
  assign mem_wreg_o = mem_wreg_i;
endmodule

module memwb_reg (
  input  mem_mreg,
  input  mem_whilo,
  input  mem_wreg,
  input  [4:0] mem_wa,
  input  [31:0] mem_hi,
  input  [31:0] mem_lo,
  input  [31:0] mem_dreg,
  input  [3:0] mem_dre,
  input  [31:0] mem_dm,
  input  rst,
  input  clk,
  output wb_mreg,
  output wb_whilo,
  output wb_wreg,
  output [4:0] wb_wa,
  output [31:0] wb_hi,
  output [31:0] wb_lo,
  output [31:0] wb_dreg,
  output [3:0] wb_dre,
  output [31:0] wb_dm
);

  wire not_1_out;

  not not_1 (not_1_out, rst);
  Register #(.width(1)) register_1 (.D(mem_mreg), .en(rst), .Q(wb_mreg), .clk(clk), .clr(not_1_out));
  Register #(.width(1)) register_2 (.D(mem_whilo), .en(rst), .Q(wb_whilo), .clk(clk), .clr(not_1_out));
  Register #(.width(1)) register_3 (.D(mem_wreg), .en(rst), .Q(wb_wreg), .clk(clk), .clr(not_1_out));
  Register #(.width(5)) register_4 (.D(mem_wa), .en(rst), .Q(wb_wa), .clk(clk), .clr(not_1_out));
  Register #(.width(32)) register_5 (.D(mem_hi), .en(rst), .Q(wb_hi), .clk(clk), .clr(not_1_out));
  Register #(.width(32)) register_6 (.D(mem_lo), .en(rst), .Q(wb_lo), .clk(clk), .clr(not_1_out));
  Register #(.width(32)) register_7 (.D(mem_dreg), .en(rst), .Q(wb_dreg), .clk(clk), .clr(not_1_out));
  Register #(.width(4)) register_8 (.D(mem_dre), .en(rst), .Q(wb_dre), .clk(clk), .clr(not_1_out));
  Register #(.width(32)) register_9 (.D(mem_dm), .en(rst), .Q(wb_dm), .clk(clk), .clr(not_1_out));
endmodule

module wb (
  input  wb_mreg_i,
  input  wb_whilo_i,
  input  wb_wreg_i,
  input  [4:0] wb_wa_i,
  input  [31:0] wb_hi_i,
  input  [31:0] wb_lo_i,
  input  [31:0] wb_dreg_i,
  input  [3:0] wb_dre_i,
  input  [31:0] dm,
  input  clk,
  output wb2exe_whilo,
  output wb_whilo_o,
  output wb_wreg_o,
  output [4:0] wb_wa_o,
  output [31:0] wb_hi_o,
  output [31:0] wb_lo_o,
  output [31:0] wb2exe_hi,
  output [31:0] wb_wd_o,
  output [31:0] wb2exe_lo
);

  wire and_1_out, priority_encoder_1_gs;
  wire [1:0] priority_encoder_1_out;
  wire [7:0] multiplexer_1_out;
  wire [31:0] bit_extender_1_out, multiplexer_2_out;

  Priority_Encoder #(.select(2)) priority_encoder_1 (
    .in0(wb_dre_i[0]), .in1(wb_dre_i[1]), .in2(wb_dre_i[2]), .in3(wb_dre_i[3]), .out(priority_encoder_1_out),
    .gs(priority_encoder_1_gs), .en_in(1'b1));  // open: en_out
  and and_1 (and_1_out, wb_dre_i[0], wb_dre_i[1], wb_dre_i[2], wb_dre_i[3]);
  Multiplexer #(.select(2), .width(8)) multiplexer_1 (
    .in0(dm[7:0]), .in1(dm[15:8]), .in2(dm[23:16]), .in3(dm[31:24]), .out(multiplexer_1_out),
    .sel(priority_encoder_1_out), .en(priority_encoder_1_gs));
  assign bit_extender_1_out = {{24{multiplexer_1_out[7]}}, multiplexer_1_out};  // Bit_Extender bit_extender_1
  Multiplexer #(.width(32), .enable("false")) multiplexer_2 (
    .in0(bit_extender_1_out), .in1({dm[7:0], dm[15:8], dm[23:16], dm[31:24]}), .out(multiplexer_2_out),
    .sel(and_1_out));
  Multiplexer #(.width(32), .enable("false")) multiplexer_3 (
    .in0(wb_dreg_i), .in1(multiplexer_2_out), .out(wb_wd_o), .sel(wb_mreg_i));

  assign wb2exe_hi = wb_hi_i;
  assign wb2exe_lo = wb_lo_i;
  assign wb2exe_whilo = wb_whilo_i;
  assign wb_hi_o = wb_hi_i;
  assign wb_lo_o = wb_lo_i;
  assign wb_wa_o = wb_wa_i;
  assign wb_whilo_o = wb_whilo_i;
  assign wb_wreg_o = wb_wreg_i;
endmodule

module DCU (
  input  equ,
  input  [5:0] op,
  input  [5:0] func,
  input  [4:0] rs,
  input  [4:0] rt,
  input  [4:0] exe2id_wa,
  input  [4:0] mem2id_wa,
  input  exe2id_wreg,
  input  mem2id_wreg,
  output [7:0] aluop,
  output [2:0] alutype,
  output rreg1,
  output rreg2,
  output wreg,
  output whilo,
  output immsel,
  output rtsel,
  output sext,
  output upper,
  output mreg,
  output shift,
  output jal,
  output [1:0] jtsel,
  output [1:0] fwrd1,
  output [1:0] fwrd2
);

  wire dcu_inst_imm_1_inst_addiu, dcu_inst_imm_1_inst_beq, dcu_inst_imm_1_inst_bne, dcu_inst_imm_1_inst_j,
       dcu_inst_imm_1_inst_jal, dcu_inst_imm_1_inst_lb, dcu_inst_imm_1_inst_lui, dcu_inst_imm_1_inst_lw,
       dcu_inst_imm_1_inst_ori, dcu_inst_imm_1_inst_sb, dcu_inst_imm_1_inst_sltiu, dcu_inst_imm_1_inst_sw,
       dcu_inst_reg_1_inst_add, dcu_inst_reg_1_inst_and, dcu_inst_reg_1_inst_div, dcu_inst_reg_1_inst_jr,
       dcu_inst_reg_1_inst_mfhi, dcu_inst_reg_1_inst_mflo, dcu_inst_reg_1_inst_mult, dcu_inst_reg_1_inst_sll,
       dcu_inst_reg_1_inst_slt, dcu_inst_reg_1_inst_subu, nor_1_out;

  nor nor_1 (nor_1_out, op[0], op[1], op[2], op[3], op[4], op[5]);
  DCU_inst_imm dcu_inst_imm_1 (
    .op0(op[0]), .op1(op[1]), .op2(op[2]), .op3(op[3]), .op4(op[4]), .op5(op[5]),
    .inst_addiu(dcu_inst_imm_1_inst_addiu), .inst_sltiu(dcu_inst_imm_1_inst_sltiu),
    .inst_ori(dcu_inst_imm_1_inst_ori), .inst_lui(dcu_inst_imm_1_inst_lui), .inst_lb(dcu_inst_imm_1_inst_lb),
    .inst_lw(dcu_inst_imm_1_inst_lw), .inst_sb(dcu_inst_imm_1_inst_sb), .inst_sw(dcu_inst_imm_1_inst_sw),
    .inst_j(dcu_inst_imm_1_inst_j), .inst_jal(dcu_inst_imm_1_inst_jal), .inst_beq(dcu_inst_imm_1_inst_beq),
    .inst_bne(dcu_inst_imm_1_inst_bne));
  DCU_inst_reg dcu_inst_reg_1 (
    .inst_reg(nor_1_out), .func0(func[0]), .func1(func[1]), .func2(func[2]), .func3(func[3]),
    .func4(func[4]), .func5(func[5]), .inst_add(dcu_inst_reg_1_inst_add),
    .inst_subu(dcu_inst_reg_1_inst_subu), .inst_slt(dcu_inst_reg_1_inst_slt),
    .inst_and(dcu_inst_reg_1_inst_and), .inst_mult(dcu_inst_reg_1_inst_mult),
    .inst_mfhi(dcu_inst_reg_1_inst_mfhi), .inst_mflo(dcu_inst_reg_1_inst_mflo),
    .inst_sll(dcu_inst_reg_1_inst_sll), .inst_jr(dcu_inst_reg_1_inst_jr), .inst_div(dcu_inst_reg_1_inst_div));
  DCU_aluop dcu_aluop_1 (
    .inst_add(dcu_inst_reg_1_inst_add), .inst_subu(dcu_inst_reg_1_inst_subu),
    .inst_slt(dcu_inst_reg_1_inst_slt), .inst_and(dcu_inst_reg_1_inst_and),
    .inst_mult(dcu_inst_reg_1_inst_mult), .inst_mfhi(dcu_inst_reg_1_inst_mfhi),
    .inst_mflo(dcu_inst_reg_1_inst_mflo), .inst_sll(dcu_inst_reg_1_inst_sll),
    .inst_addiu(dcu_inst_imm_1_inst_addiu), .inst_sltiu(dcu_inst_imm_1_inst_sltiu),
    .inst_ori(dcu_inst_imm_1_inst_ori), .inst_lui(dcu_inst_imm_1_inst_lui), .inst_lb(dcu_inst_imm_1_inst_lb),
    .inst_lw(dcu_inst_imm_1_inst_lw), .inst_sb(dcu_inst_imm_1_inst_sb), .inst_sw(dcu_inst_imm_1_inst_sw),
    .aluop0(aluop[0]), .aluop1(aluop[1]), .aluop2(aluop[2]), .aluop3(aluop[3]), .aluop4(aluop[4]),
    .aluop5(aluop[5]), .aluop6(aluop[6]), .aluop7(aluop[7]), .inst_j(dcu_inst_imm_1_inst_j),
    .inst_jal(dcu_inst_imm_1_inst_jal), .inst_jr(dcu_inst_reg_1_inst_jr), .inst_beq(dcu_inst_imm_1_inst_beq),
    .inst_bne(dcu_inst_imm_1_inst_bne), .inst_div(dcu_inst_reg_1_inst_div));
  DCU_alutype dcu_alutype_1 (
    .alutype0(alutype[0]), .alutype1(alutype[1]), .alutype2(alutype[2]), .inst_add(dcu_inst_reg_1_inst_add),
    .inst_subu(dcu_inst_reg_1_inst_subu), .inst_slt(dcu_inst_reg_1_inst_slt),
    .inst_and(dcu_inst_reg_1_inst_and), .inst_mult(dcu_inst_reg_1_inst_mult),
    .inst_mfhi(dcu_inst_reg_1_inst_mfhi), .inst_mflo(dcu_inst_reg_1_inst_mflo),
    .inst_sll(dcu_inst_reg_1_inst_sll), .inst_addiu(dcu_inst_imm_1_inst_addiu),
    .inst_sltiu(dcu_inst_imm_1_inst_sltiu), .inst_ori(dcu_inst_imm_1_inst_ori),
    .inst_lui(dcu_inst_imm_1_inst_lui), .inst_lb(dcu_inst_imm_1_inst_lb), .inst_lw(dcu_inst_imm_1_inst_lw),
    .inst_sb(dcu_inst_imm_1_inst_sb), .inst_sw(dcu_inst_imm_1_inst_sw), .inst_j(dcu_inst_imm_1_inst_j),
    .inst_jal(dcu_inst_imm_1_inst_jal), .inst_jr(dcu_inst_reg_1_inst_jr), .inst_beq(dcu_inst_imm_1_inst_beq),
    .inst_bne(dcu_inst_imm_1_inst_bne), .inst_div(dcu_inst_reg_1_inst_div));
  DCU_reg dcu_reg_1 (
    .rreg1(rreg1), .rreg2(rreg2), .wreg(wreg), .whilo(whilo), .inst_add(dcu_inst_reg_1_inst_add),
    .inst_subu(dcu_inst_reg_1_inst_subu), .inst_slt(dcu_inst_reg_1_inst_slt),
    .inst_and(dcu_inst_reg_1_inst_and), .inst_mult(dcu_inst_reg_1_inst_mult),
    .inst_mfhi(dcu_inst_reg_1_inst_mfhi), .inst_mflo(dcu_inst_reg_1_inst_mflo),
    .inst_sll(dcu_inst_reg_1_inst_sll), .inst_addiu(dcu_inst_imm_1_inst_addiu),
    .inst_sltiu(dcu_inst_imm_1_inst_sltiu), .inst_ori(dcu_inst_imm_1_inst_ori),
    .inst_lui(dcu_inst_imm_1_inst_lui), .inst_lb(dcu_inst_imm_1_inst_lb), .inst_lw(dcu_inst_imm_1_inst_lw),
    .inst_sb(dcu_inst_imm_1_inst_sb), .inst_sw(dcu_inst_imm_1_inst_sw), .inst_j(dcu_inst_imm_1_inst_j),
    .inst_jal(dcu_inst_imm_1_inst_jal), .inst_jr(dcu_inst_reg_1_inst_jr), .inst_beq(dcu_inst_imm_1_inst_beq),
    .inst_bne(dcu_inst_imm_1_inst_bne), .inst_div(dcu_inst_reg_1_inst_div));
  DCU_other dcu_other_1 (
    .immsel(immsel), .rtsel(rtsel), .sext(sext), .upper(upper), .mreg(mreg), .shift(shift),
    .inst_add(dcu_inst_reg_1_inst_add), .inst_subu(dcu_inst_reg_1_inst_subu),
    .inst_slt(dcu_inst_reg_1_inst_slt), .inst_and(dcu_inst_reg_1_inst_and),
    .inst_mult(dcu_inst_reg_1_inst_mult), .inst_mfhi(dcu_inst_reg_1_inst_mfhi),
    .inst_mflo(dcu_inst_reg_1_inst_mflo), .inst_sll(dcu_inst_reg_1_inst_sll),
    .inst_addiu(dcu_inst_imm_1_inst_addiu), .inst_sltiu(dcu_inst_imm_1_inst_sltiu),
    .inst_ori(dcu_inst_imm_1_inst_ori), .inst_lui(dcu_inst_imm_1_inst_lui), .inst_lb(dcu_inst_imm_1_inst_lb),
    .inst_lw(dcu_inst_imm_1_inst_lw), .inst_sb(dcu_inst_imm_1_inst_sb), .inst_sw(dcu_inst_imm_1_inst_sw),
    .inst_j(dcu_inst_imm_1_inst_j), .inst_jal(dcu_inst_imm_1_inst_jal), .inst_jr(dcu_inst_reg_1_inst_jr),
    .inst_beq(dcu_inst_imm_1_inst_beq), .inst_bne(dcu_inst_imm_1_inst_bne), .inst_div(dcu_inst_reg_1_inst_div));
  DCU_jump dcu_jump_1 (
    .inst_j(dcu_inst_imm_1_inst_j), .inst_jal(dcu_inst_imm_1_inst_jal), .inst_jr(dcu_inst_reg_1_inst_jr),
    .inst_beq(dcu_inst_imm_1_inst_beq), .inst_bne(dcu_inst_imm_1_inst_bne), .equ(equ), .jal(jal),
    .jtsel1(jtsel[1]), .jtsel0(jtsel[0]));
  DCU_fwrd dcu_fwrd_1 (
    .rreg1(rreg1), .rs(rs), .exe2id_wa(exe2id_wa), .mem2id_wa(mem2id_wa), .exe2id_wreg(exe2id_wreg),
    .mem2id_wreg(mem2id_wreg), .rt(rt), .rreg2(rreg2), .fwrd1(fwrd1), .fwrd2(fwrd2));
endmodule

module DCU_inst_reg (
  input  inst_reg,
  input  func0,
  input  func1,
  input  func2,
  input  func3,
  input  func4,
  input  func5,
  output inst_add,
  output inst_subu,
  output inst_slt,
  output inst_and,
  output inst_mult,
  output inst_mfhi,
  output inst_mflo,
  output inst_sll,
  output inst_jr,
  output inst_div
);

  wire not_1_out, not_2_out, not_3_out, not_4_out, not_5_out, not_6_out, not_7_out, not_8_out, not_9_out,
       not_10_out, not_11_out, not_12_out, not_13_out, not_14_out, not_15_out, not_16_out, not_17_out,
       not_18_out, not_19_out, not_20_out, not_21_out, not_22_out, not_23_out, not_24_out, not_25_out,
       not_26_out, not_27_out, not_28_out, not_29_out, not_30_out, not_31_out, not_32_out, not_33_out,
       not_34_out, not_35_out, not_36_out, not_37_out, not_38_out, not_39_out, not_40_out, not_41_out,
       not_42_out;

  not not_1 (not_1_out, func4);
  not not_2 (not_2_out, func3);
  not not_3 (not_3_out, func2);
  not not_4 (not_4_out, func1);
  not not_5 (not_5_out, func0);
  not not_6 (not_6_out, func4);
  not not_7 (not_7_out, func3);
  not not_8 (not_8_out, func2);
  not not_9 (not_9_out, func4);
  not not_10 (not_10_out, func2);
  not not_11 (not_11_out, func0);
  not not_12 (not_12_out, func4);
  not not_13 (not_13_out, func3);
  not not_14 (not_14_out, func1);
  not not_15 (not_15_out, func0);
  not not_16 (not_16_out, func5);
  not not_17 (not_17_out, func2);
  not not_18 (not_18_out, func1);
  not not_19 (not_19_out, func0);
  not not_20 (not_20_out, func5);
  not not_21 (not_21_out, func3);
  not not_22 (not_22_out, func2);
  not not_23 (not_23_out, func1);
  not not_24 (not_24_out, func0);
  not not_25 (not_25_out, func5);
  not not_26 (not_26_out, func3);
  not not_27 (not_27_out, func2);
  not not_28 (not_28_out, func0);
  not not_29 (not_29_out, func5);
  not not_30 (not_30_out, func4);
  not not_31 (not_31_out, func3);
  not not_32 (not_32_out, func2);
  not not_33 (not_33_out, func1);
  not not_34 (not_34_out, func0);
  not not_35 (not_35_out, func5);
  not not_36 (not_36_out, func4);
  not not_37 (not_37_out, func2);
  not not_38 (not_38_out, func1);
  not not_39 (not_39_out, func0);
  not not_40 (not_40_out, func5);
  not not_41 (not_41_out, func2);
  not not_42 (not_42_out, func0);
  and and_1 (inst_add, inst_reg, func5, not_1_out, not_2_out, not_3_out, not_4_out, not_5_out);
  and and_2 (inst_subu, inst_reg, func5, not_6_out, not_7_out, not_8_out, func1, func0);
  and and_3 (inst_slt, inst_reg, func5, not_9_out, func3, not_10_out, func1, not_11_out);
  and and_4 (inst_and, inst_reg, func5, not_12_out, not_13_out, func2, not_14_out, not_15_out);
  and and_5 (inst_mult, inst_reg, not_16_out, func4, func3, not_17_out, not_18_out, not_19_out);
  and and_6 (inst_mfhi, inst_reg, not_20_out, func4, not_21_out, not_22_out, not_23_out, not_24_out);
  and and_7 (inst_mflo, inst_reg, not_25_out, func4, not_26_out, not_27_out, func1, not_28_out);
  and and_8 (inst_sll, inst_reg, not_29_out, not_30_out, not_31_out, not_32_out, not_33_out, not_34_out);
  and and_9 (inst_jr, inst_reg, not_35_out, not_36_out, func3, not_37_out, not_38_out, not_39_out);
  and and_10 (inst_div, inst_reg, not_40_out, func4, func3, not_41_out, func1, not_42_out);
endmodule

module DCU_inst_imm (
  input  op0,
  input  op1,
  input  op2,
  input  op3,
  input  op4,
  input  op5,
  output inst_addiu,
  output inst_sltiu,
  output inst_ori,
  output inst_lui,
  output inst_lb,
  output inst_lw,
  output inst_sb,
  output inst_sw,
  output inst_j,
  output inst_jal,
  output inst_beq,
  output inst_bne
);

  wire not_1_out, not_2_out, not_3_out, not_4_out, not_5_out, not_6_out, not_7_out, not_8_out, not_9_out,
       not_10_out, not_11_out, not_12_out, not_13_out, not_14_out, not_15_out, not_16_out, not_17_out,
       not_18_out, not_19_out, not_20_out, not_21_out, not_22_out, not_23_out, not_24_out, not_25_out,
       not_26_out, not_27_out, not_28_out, not_29_out, not_30_out, not_31_out, not_32_out, not_33_out,
       not_34_out, not_35_out, not_36_out, not_37_out, not_38_out, not_39_out, not_40_out, not_41_out,
       not_42_out, not_43_out, not_44_out;

  not not_1 (not_1_out, op5);
  not not_2 (not_2_out, op4);
  not not_3 (not_3_out, op2);
  not not_4 (not_4_out, op1);
  not not_5 (not_5_out, op5);
  not not_6 (not_6_out, op4);
  not not_7 (not_7_out, op2);
  not not_8 (not_8_out, op5);
  not not_9 (not_9_out, op4);
  not not_10 (not_10_out, op1);
  not not_11 (not_11_out, op5);
  not not_12 (not_12_out, op4);
  not not_13 (not_13_out, op4);
  not not_14 (not_14_out, op3);
  not not_15 (not_15_out, op2);
  not not_16 (not_16_out, op1);
  not not_17 (not_17_out, op0);
  not not_18 (not_18_out, op4);
  not not_19 (not_19_out, op3);
  not not_20 (not_20_out, op2);
  not not_21 (not_21_out, op4);
  not not_22 (not_22_out, op2);
  not not_23 (not_23_out, op1);
  not not_24 (not_24_out, op0);
  not not_25 (not_25_out, op4);
  not not_26 (not_26_out, op2);
  not not_27 (not_27_out, op5);
  not not_28 (not_28_out, op4);
  not not_29 (not_29_out, op3);
  not not_30 (not_30_out, op2);
  not not_31 (not_31_out, op0);
  not not_32 (not_32_out, op5);
  not not_33 (not_33_out, op4);
  not not_34 (not_34_out, op3);
  not not_35 (not_35_out, op2);
  not not_36 (not_36_out, op5);
  not not_37 (not_37_out, op4);
  not not_38 (not_38_out, op3);
  not not_39 (not_39_out, op1);
  not not_40 (not_40_out, op0);
  not not_41 (not_41_out, op5);
  not not_42 (not_42_out, op4);
  not not_43 (not_43_out, op3);
  not not_44 (not_44_out, op1);
  and and_1 (inst_addiu, not_1_out, not_2_out, op3, not_3_out, not_4_out, op0);
  and and_2 (inst_sltiu, not_5_out, not_6_out, op3, not_7_out, op1, op0);
  and and_3 (inst_ori, not_8_out, not_9_out, op3, op2, not_10_out, op0);
  and and_4 (inst_lui, not_11_out, not_12_out, op3, op2, op1, op0);
  and and_5 (inst_lb, op5, not_13_out, not_14_out, not_15_out, not_16_out, not_17_out);
  and and_6 (inst_lw, op5, not_18_out, not_19_out, not_20_out, op1, op0);
  and and_7 (inst_sb, op5, not_21_out, op3, not_22_out, not_23_out, not_24_out);
  and and_8 (inst_sw, op5, not_25_out, op3, not_26_out, op1, op0);
  and and_9 (inst_j, not_27_out, not_28_out, not_29_out, not_30_out, op1, not_31_out);
  and and_10 (inst_jal, not_32_out, not_33_out, not_34_out, not_35_out, op1, op0);
  and and_11 (inst_beq, not_36_out, not_37_out, not_38_out, op2, not_39_out, not_40_out);
  and and_12 (inst_bne, not_41_out, not_42_out, not_43_out, op2, not_44_out, op0);
endmodule

module DCU_aluop (
  input  inst_add,
  input  inst_subu,
  input  inst_slt,
  input  inst_and,
  input  inst_mult,
  input  inst_mfhi,
  input  inst_mflo,
  input  inst_sll,
  input  inst_addiu,
  input  inst_sltiu,
  input  inst_ori,
  input  inst_lui,
  input  inst_lb,
  input  inst_lw,
  input  inst_sb,
  input  inst_sw,
  input  inst_j,
  input  inst_jal,
  input  inst_jr,
  input  inst_beq,
  input  inst_bne,
  input  inst_div,
  output aluop0,
  output aluop1,
  output aluop2,
  output aluop3,
  output aluop4,
  output aluop5,
  output aluop6,
  output aluop7
);

  or or_1 (aluop0, inst_subu, inst_mflo, inst_sll, inst_addiu, inst_sltiu, inst_ori, inst_lui, inst_jr, inst_bne);
  or or_2 (aluop1, inst_subu, inst_slt, inst_sltiu, inst_lw, inst_sw, inst_jal, inst_div);
  or or_3 (aluop2, inst_and, inst_slt, inst_mult, inst_mfhi, inst_mflo, inst_sltiu, inst_ori, inst_lui, inst_j, inst_jal, inst_jr, inst_div);
  or or_4 (aluop3, inst_add, inst_subu, inst_and, inst_mfhi, inst_mflo, inst_addiu, inst_ori, inst_sb, inst_sw, inst_j, inst_jal, inst_jr);
  or or_5 (aluop4, inst_add, inst_subu, inst_and, inst_mult, inst_sll, inst_addiu, inst_ori, inst_lb, inst_lw, inst_sb, inst_sw, inst_beq, inst_bne, inst_div);
  or or_6 (aluop5, inst_slt, inst_sltiu, inst_j, inst_jal, inst_jr, inst_beq, inst_bne);
  or or_7 (aluop7, inst_lb, inst_lw, inst_sb, inst_sw);

  assign aluop6 = 1'b0;
endmodule

module DCU_reg (
  input  inst_add,
  input  inst_subu,
  input  inst_slt,
  input  inst_and,
  input  inst_mult,
  input  inst_mfhi,
  input  inst_mflo,
  input  inst_sll,
  input  inst_addiu,
  input  inst_sltiu,
  input  inst_ori,
  input  inst_lui,
  input  inst_lb,
  input  inst_lw,
  input  inst_sb,
  input  inst_sw,
  input  inst_j,
  input  inst_jal,
  input  inst_jr,
  input  inst_beq,
  input  inst_bne,
  input  inst_div,
  output rreg1,
  output rreg2,
  output wreg,
  output whilo
);

  or or_1 (rreg1, inst_add, inst_subu, inst_slt, inst_and, inst_mult, inst_addiu, inst_sltiu, inst_ori, inst_lb, inst_lw, inst_sb, inst_sw, inst_jr, inst_beq, inst_bne, inst_div);
  or or_2 (rreg2, inst_add, inst_subu, inst_slt, inst_and, inst_mult, inst_sll, inst_sb, inst_sw, inst_beq, inst_bne, inst_div);
  or or_3 (wreg, inst_add, inst_subu, inst_slt, inst_and, inst_mfhi, inst_mflo, inst_sll, inst_addiu, inst_sltiu, inst_ori, inst_lui, inst_lb, inst_lw, inst_jr);
  or or_4 (whilo, inst_mult, inst_div);
endmodule

module DCU_alutype (
  input  inst_add,
  input  inst_subu,
  input  inst_slt,
  input  inst_and,
  input  inst_mult,
  input  inst_mfhi,
  input  inst_mflo,
  input  inst_sll,
  input  inst_addiu,
  input  inst_sltiu,
  input  inst_ori,
  input  inst_lui,
  input  inst_lb,
  input  inst_lw,
  input  inst_sb,
  input  inst_sw,
  input  inst_j,
  input  inst_jal,
  input  inst_jr,
  input  inst_beq,
  input  inst_bne,
  input  inst_div,
  output alutype0,
  output alutype1,
  output alutype2
);

  or or_1 (alutype0, inst_add, inst_subu, inst_slt, inst_mfhi, inst_mflo, inst_addiu, inst_sltiu, inst_lb, inst_lw, inst_sb, inst_sw, inst_j, inst_jal, inst_jr, inst_beq, inst_bne);
  or or_2 (alutype1, inst_and, inst_mfhi, inst_mflo, inst_ori, inst_lui);
  or or_3 (alutype2, inst_sll, inst_j, inst_jal, inst_jr, inst_beq, inst_bne);
endmodule

module DCU_other (
  input  inst_add,
  input  inst_subu,
  input  inst_slt,
  input  inst_and,
  input  inst_mult,
  input  inst_mfhi,
  input  inst_mflo,
  input  inst_sll,
  input  inst_addiu,
  input  inst_sltiu,
  input  inst_ori,
  input  inst_lui,
  input  inst_lb,
  input  inst_lw,
  input  inst_sb,
  input  inst_sw,
  input  inst_j,
  input  inst_jal,
  input  inst_jr,
  input  inst_beq,
  input  inst_bne,
  input  inst_div,
  output immsel,
  output rtsel,
  output sext,
  output upper,
  output mreg,
  output shift
);

  or or_1 (immsel, inst_addiu, inst_sltiu, inst_ori, inst_lui, inst_lb, inst_lw, inst_sb, inst_sw);
  or or_2 (rtsel, inst_addiu, inst_sltiu, inst_ori, inst_lui, inst_lb, inst_lw, inst_sb, inst_sw);
  or or_3 (sext, inst_addiu, inst_sltiu, inst_lb, inst_lw, inst_sb, inst_sw);
  or or_4 (mreg, inst_lb, inst_lw);

  assign shift = inst_sll;
  assign upper = inst_lui;
endmodule

module DCU_fwrd (
  input  rreg1,
  input  [4:0] rs,
  input  [4:0] exe2id_wa,
  input  [4:0] mem2id_wa,
  input  exe2id_wreg,
  input  mem2id_wreg,
  input  [4:0] rt,
  input  rreg2,
  output [1:0] fwrd1,
  output [1:0] fwrd2
);

  wire nor_1_out, nor_2_out, nor_3_out, nor_4_out;
  wire [4:0] xor_1_out, xor_2_out, xor_3_out, xor_4_out;

  assign xor_1_out = rs ^ exe2id_wa;  // XOR_Gate xor_1, 5 bits wide
  assign xor_2_out = rs ^ mem2id_wa;  // XOR_Gate xor_2, 5 bits wide
  assign xor_3_out = rt ^ exe2id_wa;  // XOR_Gate xor_3, 5 bits wide
  assign xor_4_out = rt ^ mem2id_wa;  // XOR_Gate xor_4, 5 bits wide
  nor nor_1 (nor_1_out, xor_1_out[0], xor_1_out[1], xor_1_out[2], xor_1_out[3], xor_1_out[4]);
  nor nor_2 (nor_2_out, xor_2_out[0], xor_2_out[1], xor_2_out[2], xor_2_out[3], xor_2_out[4]);
  nor nor_3 (nor_3_out, xor_3_out[0], xor_3_out[1], xor_3_out[2], xor_3_out[3], xor_3_out[4]);
  nor nor_4 (nor_4_out, xor_4_out[0], xor_4_out[1], xor_4_out[2], xor_4_out[3], xor_4_out[4]);
  and and_1 (fwrd1[0], rreg1, exe2id_wreg, nor_1_out);
  and and_2 (fwrd1[1], rreg1, nor_2_out, mem2id_wreg);
  and and_3 (fwrd2[0], nor_3_out, exe2id_wreg, rreg2);
  and and_4 (fwrd2[1], nor_4_out, mem2id_wreg, rreg2);
endmodule

module DCU_jump (
  input  inst_j,
  input  inst_jal,
  input  inst_jr,
  input  inst_beq,
  input  inst_bne,
  input  equ,
  output jal,
  output jtsel1,
  output jtsel0
);

  wire and_1_out, and_2_out, not_1_out;

  not not_1 (not_1_out, equ);
  and and_1 (and_1_out, inst_beq, equ);
  and and_2 (and_2_out, inst_bne, not_1_out);
  or or_1 (jtsel1, inst_j, inst_jal, and_1_out, and_2_out);
  or or_2 (jtsel0, inst_jr, and_1_out, and_2_out);

  assign jal = inst_jal;
endmodule

module HILO (
  input  we,
  input  [31:0] in_2,
  input  [31:0] in_3,
  input  clk,
  output [31:0] out_5,
  output [31:0] out_6
);

  Register #(.width(32)) hi (.D(in_2), .en(we), .Q(out_5), .clk(clk));  // open: clr
  Register #(.width(32)) lo (.D(in_3), .en(we), .Q(out_6), .clk(clk));  // open: clr
endmodule

module ALU (
  input  [7:0] aluop,
  input  [31:0] src1,
  input  [31:0] src2,
  input  clk,
  output [31:0] logicres,
  output [31:0] arithres,
  output [31:0] shiftres,
  output [31:0] mulres_lo,
  output [31:0] mulres_hi,
  output stallreq_exe,
  output [31:0] divres_hi,
  output [31:0] divres_lo
);

  wire [4:0] bitselector_1_out;
  wire [31:0] shifter_1_out;

  BitSelector #(.width(32), .group(5)) bitselector_1 (.in(src1), .out(bitselector_1_out), .sel(3'b000));
  ALU_logicres alu_logicres_1 (.aluop(aluop), .src1(src1), .src2(src2), .logicres(logicres));
  ALU_arithres alu_arithres_1 (.aluop(aluop), .src1(src1), .src2(src2), .logicres(arithres));
  Shifter #(.width(32)) shifter_1 (.in(src2), .\dist (bitselector_1_out), .out(shifter_1_out));
  Multiplier #(.width(32)) multiplier_1 (.a(src1), .b(src2), .out(mulres_lo), .cout(mulres_hi));  // open: cin
  ALU_divres alu_divres_1 (
    .aluop(aluop), .src1(src1), .src2(src2), .clk(clk), .stallreq_exe(stallreq_exe), .divres_hi(divres_hi),
    .divres_lo(divres_lo));
  EqualMux equalmux_1 (.src(shifter_1_out), .en1(8'h11), .en2(aluop), .out_4(shiftres));

  // Notes on the sheet:
  //   divres
endmodule

module ALU_logicres (
  input  [7:0] aluop,
  input  [31:0] src1,
  input  [31:0] src2,
  output [31:0] logicres
);

  wire [31:0] and_1_out, equalmux_1_out_4, equalmux_2_out_4, equalmux_3_out_4, or_1_out;

  assign and_1_out = src1 & src2;  // AND_Gate and_1, 32 bits wide
  assign or_1_out = src1 | src2;  // OR_Gate or_1, 32 bits wide
  EqualMux equalmux_1 (.src(and_1_out), .en1(8'h1c), .en2(aluop), .out_4(equalmux_1_out_4));
  EqualMux equalmux_2 (.src(or_1_out), .en1(8'h1d), .en2(aluop), .out_4(equalmux_2_out_4));
  EqualMux equalmux_3 (.src(src2), .en1(8'h5), .en2(aluop), .out_4(equalmux_3_out_4));
  assign logicres = equalmux_1_out_4 | equalmux_2_out_4 | equalmux_3_out_4;  // OR_Gate or_2, 32 bits wide
endmodule

module ALU_arithres (
  input  [7:0] aluop,
  input  [31:0] src1,
  input  [31:0] src2,
  output [31:0] logicres
);

  wire comparator_1_lt, comparator_2_lt;
  wire [31:0] adder_1_out, adder_2_out, adder_3_out, bit_extender_1_out, bit_extender_2_out,
       equalmux_1_out_4, equalmux_2_out_4, equalmux_3_out_4, equalmux_4_out_4, equalmux_5_out_4,
       equalmux_6_p5, equalmux_7_p4, equalmux_8_out_4, equalmux_9_out_4, subtractor_1_out;

  Adder #(.width(32)) adder_1 (.a(src1), .b(src2), .out(adder_1_out));  // open: cin, cout
  Subtractor #(.width(32)) subtractor_1 (.a(src1), .b(src2), .out(subtractor_1_out));  // open: bin, bout
  Comparator #(.width(32)) comparator_1 (.a(src1), .b(src2), .lt(comparator_1_lt));  // open: gt, eq
  Adder #(.width(32)) adder_2 (.a(src1), .b(src2), .out(adder_2_out));  // open: cin, cout
  Comparator #(.width(32), .mode("unsigned")) comparator_2 (.a(src1), .b(src2), .lt(comparator_2_lt));  // open: gt, eq
  Adder #(.width(32)) adder_3 (.a(src1), .b(src2), .out(adder_3_out));  // open: cin, cout
  assign bit_extender_1_out = {{31{1'b0}}, comparator_1_lt};  // Bit_Extender bit_extender_1
  assign bit_extender_2_out = {{31{1'b0}}, comparator_2_lt};  // Bit_Extender bit_extender_2
  EqualMux equalmux_1 (.src(adder_1_out), .en1(8'h18), .en2(aluop), .out_4(equalmux_1_out_4));
  EqualMux equalmux_2 (.src(subtractor_1_out), .en1(8'h1b), .en2(aluop), .out_4(equalmux_2_out_4));
  EqualMux equalmux_3 (.src(bit_extender_1_out), .en1(8'h26), .en2(aluop), .out_4(equalmux_3_out_4));
  EqualMux equalmux_4 (.src(adder_2_out), .en1(8'h19), .en2(aluop), .out_4(equalmux_4_out_4));
  EqualMux equalmux_5 (.src(bit_extender_2_out), .en1(8'h27), .en2(aluop), .out_4(equalmux_5_out_4));
  // EqualMux equalmux_6: pin names not known; wires that end beside it: adder_3_out, 8'h90, aluop, adder_3_out, equalmux_6_p5
  // EqualMux equalmux_7: pin names not known; wires that end beside it: adder_3_out, 8'h92, aluop, equalmux_7_p4
  EqualMux equalmux_8 (.src(adder_3_out), .en1(8'h98), .en2(aluop), .out_4(equalmux_8_out_4));
  EqualMux equalmux_9 (.src(adder_3_out), .en1(8'h9a), .en2(aluop), .out_4(equalmux_9_out_4));
  assign logicres = equalmux_1_out_4 | equalmux_2_out_4 | equalmux_3_out_4 | equalmux_4_out_4 | equalmux_5_out_4 | equalmux_6_p5 | equalmux_7_p4 | equalmux_8_out_4 | equalmux_9_out_4;  // OR_Gate or_1, 32 bits wide
endmodule

module ALU_divres (
  input  [7:0] aluop,
  input  [31:0] src1,
  input  [31:0] src2,
  input  clk,
  output stallreq_exe,
  output [31:0] divres_hi,
  output [31:0] divres_lo
);

  wire cnt_en, comparator_1_eq, dividend_en, end_en, not_1_out, ready, ready_q, state_en, temp_op_en;
  wire [1:0] state, state_out;
  wire [5:0] cnt, cnt_out;
  wire [31:0] divres_hi_t, divres_lo_t, quotient, quotient_out, remainder, remainder_out, temp_op1,
       temp_op1_out, temp_op2, temp_op2_out;

  Comparator comparator_1 (.a(8'h16), .b(aluop), .eq(comparator_1_eq));  // open: gt, lt
  Register #(.width(1)) u_ready (.D(ready), .en(end_en), .Q(ready_q), .clk(clk));  // open: clr
  Register #(.width(2)) u_state (.D(state_out), .en(state_en), .Q(state), .clk(clk));  // open: clr
  Register #(.width(6)) u_cnt (.D(cnt_out), .en(cnt_en), .Q(cnt), .clk(clk));  // open: clr
  Register #(.width(32)) u_temp_op1 (.D(temp_op1_out), .en(temp_op_en), .Q(temp_op1), .clk(clk));  // open: clr
  Register #(.width(32)) u_temp_op2 (.D(temp_op2_out), .en(temp_op_en), .Q(temp_op2), .clk(clk));  // open: clr
  Register #(.width(32)) u_remainder (.D(remainder_out), .en(dividend_en), .Q(remainder), .clk(clk));  // open: clr
  Register #(.width(32)) u_quotient (.D(quotient_out), .en(dividend_en), .Q(quotient), .clk(clk));  // open: clr
  not not_1 (not_1_out, ready_q);
  and and_1 (stallreq_exe, comparator_1_eq, not_1_out);
  ALU_divres_state alu_divres_state_1 (
    .div_start(stallreq_exe), .state(state), .src2(src2), .cnt(cnt), .state_en(state_en),
    .state_out(state_out));
  ALU_divres_cnt alu_divres_cnt_1 (
    .cnt(cnt), .state(state), .div_start(stallreq_exe), .src2(src2), .cnt_en(cnt_en), .cnt_out(cnt_out));
  ALU_divres_op alu_divres_op_1 (
    .src1(src1), .src2(src2), .state(state), .div_start(stallreq_exe), .temp_op1(temp_op1_out),
    .temp_op2(temp_op2_out), .op_en(temp_op_en));
  ALU_divres_dividend alu_divres_dividend_1 (
    .div_start(stallreq_exe), .src2(src1), .state(state), .cnt(cnt), .temp_op1(temp_op1_out),
    .temp_op2(temp_op2), .remainder(remainder), .quotient(quotient), .src1(src2),
    .remainder_out(remainder_out), .en(dividend_en), .quotient_out(quotient_out));
  ALU_divres_end alu_divres_end_1 (
    .state(state), .div_start(stallreq_exe), .remainder(remainder), .quotient(quotient), .en(end_en),
    .ready_out(ready), .divres_hi(divres_hi_t), .divres_lo(divres_lo_t));
  Register #(.width(32)) u_divres_hi (.D(divres_hi_t), .en(end_en), .Q(divres_hi), .clk(clk));  // open: clr
  Register #(.width(32)) u_divres_lo (.D(divres_lo_t), .en(end_en), .Q(divres_lo), .clk(clk));  // open: clr

  // Other names for the same wires on the sheet: start = stallreq_exe

  // Notes on the sheet:
  //   div_free
  //   div_on
  //   div_end
  //   div_by_zero
endmodule

module ALU_divres_state (
  input  div_start,
  input  [1:0] state,
  input  [31:0] src2,
  input  [5:0] cnt,
  output state_en,
  output [1:0] state_out
);

  wire and_1_out, and_2_out, and_3_out, and_4_out, comparator_1_eq, comparator_2_eq, comparator_3_eq,
       comparator_4_eq, comparator_5_eq, comparator_6_eq, not_1_out, not_2_out;
  wire [1:0] truemux2_1_out_3, truemux2_2_out_3, truemux2_3_out_3, truemux2_4_out_3, truemux2_5_out_3;

  Comparator #(.width(2)) comparator_1 (.a(2'b11), .b(state), .eq(comparator_1_eq));  // open: gt, lt
  Comparator #(.width(2)) comparator_2 (.a(2'b00), .b(state), .eq(comparator_2_eq));  // open: gt, lt
  Comparator #(.width(2)) comparator_3 (.a(2'b01), .b(state), .eq(comparator_3_eq));  // open: gt, lt
  Comparator #(.width(2)) comparator_4 (.a(2'b10), .b(state), .eq(comparator_4_eq));  // open: gt, lt
  Comparator #(.width(32)) comparator_5 (.a({32{1'b0}}), .b(src2), .eq(comparator_5_eq));  // open: gt, lt
  Comparator #(.width(6)) comparator_6 (.a(6'b100000), .b(cnt), .eq(comparator_6_eq));  // open: gt, lt
  not not_1 (not_1_out, div_start);
  not not_2 (not_2_out, comparator_5_eq);
  and and_1 (and_1_out, comparator_1_eq, not_1_out);
  and and_2 (and_2_out, div_start, comparator_2_eq, comparator_5_eq);
  and and_3 (and_3_out, div_start, comparator_2_eq, not_2_out);
  and and_4 (and_4_out, comparator_4_eq, comparator_6_eq);
  TrueMux2 truemux2_1 (.in_1(and_1_out), .in_2(2'b00), .out_3(truemux2_1_out_3));
  TrueMux2 truemux2_2 (.in_1(and_2_out), .in_2(2'b01), .out_3(truemux2_2_out_3));
  TrueMux2 truemux2_3 (.in_1(comparator_3_eq), .in_2(2'b11), .out_3(truemux2_3_out_3));
  TrueMux2 truemux2_4 (.in_1(and_3_out), .in_2(2'b10), .out_3(truemux2_4_out_3));
  TrueMux2 truemux2_5 (.in_1(and_4_out), .in_2(2'b11), .out_3(truemux2_5_out_3));
  or or_1 (state_en, and_1_out, and_2_out, comparator_3_eq, and_3_out, and_4_out);
  assign state_out = truemux2_1_out_3 | truemux2_2_out_3 | truemux2_3_out_3 | truemux2_4_out_3 | truemux2_5_out_3;  // OR_Gate or_2, 2 bits wide

  // Notes on the sheet:
  //   div_free
  //   div_by_zero
  //   div_on
  //   div_end
endmodule

module ALU_divres_cnt (
  input  [5:0] cnt,
  input  [1:0] state,
  input  div_start,
  input  [31:0] src2,
  output cnt_en,
  output [5:0] cnt_out
);

  wire and_1_out, and_2_out, and_3_out, comparator_1_eq, comparator_2_eq, comparator_3_eq, comparator_4_eq,
       not_1_out, not_2_out;
  wire [5:0] adder_1_out, truemux6_1_out_3, truemux6_2_out_3, truemux6_3_out_3;

  Comparator #(.width(6)) comparator_1 (.a(6'b100000), .b(cnt), .eq(comparator_1_eq));  // open: gt, lt
  Comparator #(.width(2)) comparator_2 (.a(2'b10), .b(state), .eq(comparator_2_eq));  // open: gt, lt
  Comparator #(.width(2)) comparator_3 (.a(2'b00), .b(state), .eq(comparator_3_eq));  // open: gt, lt
  Comparator #(.width(32)) comparator_4 (.a({32{1'b0}}), .b(src2), .eq(comparator_4_eq));  // open: gt, lt
  not not_1 (not_1_out, comparator_4_eq);
  Adder #(.width(6)) adder_1 (.a(cnt), .b(6'b000010), .out(adder_1_out));  // open: cin, cout
  not not_2 (not_2_out, comparator_1_eq);
  and and_1 (and_1_out, comparator_2_eq, not_2_out);
  and and_2 (and_2_out, comparator_1_eq, comparator_2_eq);
  and and_3 (and_3_out, comparator_3_eq, div_start, not_1_out);
  TrueMux6 truemux6_1 (.in_1(and_1_out), .in_2(adder_1_out), .out_3(truemux6_1_out_3));
  TrueMux6 truemux6_2 (.in_1(and_2_out), .in_2({6{1'b0}}), .out_3(truemux6_2_out_3));
  TrueMux6 truemux6_3 (.in_1(and_3_out), .in_2({6{1'b0}}), .out_3(truemux6_3_out_3));
  or or_1 (cnt_en, and_1_out, and_2_out, and_3_out);
  assign cnt_out = truemux6_1_out_3 | truemux6_2_out_3 | truemux6_3_out_3;  // OR_Gate or_2, 6 bits wide
endmodule

module ALU_divres_op (
  input  [31:0] src1,
  input  [31:0] src2,
  input  [1:0] state,
  input  div_start,
  output [31:0] temp_op1,
  output [31:0] temp_op2,
  output op_en
);

  wire comparator_1_eq, comparator_2_eq, not_1_out;
  wire [31:0] negator_1_out, negator_2_out;

  Negator #(.width(32)) negator_1 (.in(src1), .out(negator_1_out));
  Negator #(.width(32)) negator_2 (.in(src2), .out(negator_2_out));
  Multiplexer #(.width(32), .enable("false")) multiplexer_1 (
    .in0(src1), .in1(negator_1_out), .out(temp_op1), .sel(src1[31]));
  Multiplexer #(.width(32), .enable("false")) multiplexer_2 (
    .in0(src2), .in1(negator_2_out), .out(temp_op2), .sel(src2[31]));
  Comparator #(.width(2)) comparator_1 (.a(2'b00), .b(state), .eq(comparator_1_eq));  // open: gt, lt
  Comparator #(.width(32)) comparator_2 (.a({32{1'b0}}), .b(src2), .eq(comparator_2_eq));  // open: gt, lt
  not not_1 (not_1_out, comparator_2_eq);
  and and_1 (op_en, comparator_1_eq, div_start, not_1_out);
endmodule

module ALU_divres_dividend (
  input  div_start,
  input  [31:0] src2,
  input  [1:0] state,
  input  [5:0] cnt,
  input  [31:0] temp_op1,
  input  [31:0] temp_op2,
  input  [31:0] remainder,
  input  [31:0] quotient,
  input  [31:0] src1,
  output [31:0] remainder_out,
  output en,
  output [31:0] quotient_out
);

  wire adder_1_cout, and_1_out, and_2_out, and_3_out, comparator_1_eq, comparator_2_eq, comparator_3_eq,
       comparator_4_eq, comparator_5_eq, comparator_6_lt, comparator_7_lt, comparator_8_lt, comparator_9_eq,
       nor_1_out, nor_2_out, not_1_out, not_2_out, not_3_out, xor_1_out, xor_2_out;
  wire [1:0] priority_encoder_1_out, priority_encoder_2_out;
  wire [31:0] adder_1_out, bit_extender_2_out, bit_extender_3_out, multiplexer_5_out, negator_1_out,
       negator_2_out, or_1_out, quotient_out1, quotient_out3, quotient_out4, remainder_out1, remainder_out3,
       remainder_out4, shifter_1_out, shifter_2_out, shifter_4_out, shifter_5_out, subtractor_1_out,
       subtractor_2_out, subtractor_3_out;

  Comparator #(.width(32)) comparator_1 (.a({32{1'b0}}), .b(src2), .eq(comparator_1_eq));  // open: gt, lt
  Comparator #(.width(2)) comparator_2 (.a(2'b00), .b(state), .eq(comparator_2_eq));  // open: gt, lt
  Comparator #(.width(2)) comparator_3 (.a(2'b01), .b(state), .eq(comparator_3_eq));  // open: gt, lt
  Comparator #(.width(2)) comparator_4 (.a(2'b10), .b(state), .eq(comparator_4_eq));  // open: gt, lt
  Comparator #(.width(6)) comparator_5 (.a(6'b100000), .b(cnt), .eq(comparator_5_eq));  // open: gt, lt
  Shifter #(.width(32)) shifter_1 (.in(temp_op2), .\dist (5'b00001), .out(shifter_1_out));
  Shifter #(.width(32)) shifter_2 (.in(temp_op2), .\dist (5'b00001), .out(shifter_2_out));
  Negator #(.width(32)) negator_1 (.in(remainder), .out(negator_1_out));
  not not_1 (not_1_out, comparator_1_eq);
  assign remainder_out1 = {{30{1'b0}}, temp_op1[31:30]};  // Bit_Extender bit_extender_1
  Shifter #(.width(32)) shifter_3 (.in(temp_op1), .\dist (5'b00010), .out(quotient_out1));
  Adder #(.width(32)) adder_1 (.a(temp_op2), .b(shifter_2_out), .out(adder_1_out), .cout(adder_1_cout));  // open: cin
  Negator #(.width(32)) negator_2 (.in(quotient), .out(negator_2_out));
  not not_2 (not_2_out, comparator_5_eq);
  xor xor_1 (xor_1_out, src1[31], src2[31]);
  xor xor_2 (xor_2_out, src1[31], remainder[31]);
  and and_1 (and_1_out, div_start, not_1_out, comparator_2_eq);
  Multiplexer #(.width(32), .enable("false")) multiplexer_1 (
    .in0(quotient), .in1(negator_2_out), .out(quotient_out4), .sel(xor_1_out));
  Multiplexer #(.width(32), .enable("false")) multiplexer_2 (
    .in0(remainder), .in1(negator_1_out), .out(remainder_out4), .sel(xor_2_out));
  and and_2 (and_2_out, comparator_4_eq, not_2_out);
  and and_3 (and_3_out, comparator_4_eq, comparator_5_eq);
  Priority_Encoder #(.select(2)) priority_encoder_1 (
    .in0(and_1_out), .in1(comparator_3_eq), .in2(and_2_out), .in3(and_3_out), .out(priority_encoder_1_out),
    .gs(en), .en_in(1'b1));  // open: en_out
  Comparator #(.width(32), .mode("unsigned")) comparator_6 (
    .a(remainder), .b(temp_op2), .lt(comparator_6_lt));  // open: gt, eq
  Comparator #(.width(32), .mode("unsigned")) comparator_7 (
    .a(remainder), .b(shifter_1_out), .lt(comparator_7_lt));  // open: gt, eq
  Comparator #(.width(32), .mode("unsigned")) comparator_8 (
    .a(remainder), .b(adder_1_out), .lt(comparator_8_lt));  // open: gt, eq
  Subtractor #(.width(32)) subtractor_1 (.a(remainder), .b(temp_op2), .out(subtractor_1_out));  // open: bin, bout
  Subtractor #(.width(32)) subtractor_2 (.a(remainder), .b(shifter_1_out), .out(subtractor_2_out));  // open: bin, bout
  Subtractor #(.width(32)) subtractor_3 (.a(remainder), .b(adder_1_out), .out(subtractor_3_out));  // open: bin, bout
  not not_3 (not_3_out, comparator_6_lt);
  nor nor_1 (nor_1_out, comparator_7_lt, temp_op2[31]);
  nor nor_2 (nor_2_out, comparator_8_lt, temp_op2[31], adder_1_cout);
  Shifter #(.width(32)) shifter_4 (.in(quotient), .\dist (5'b00010), .out(shifter_4_out));
  Multiplexer #(.select(2), .width(32), .enable("false")) multiplexer_3 (
    .in0(remainder_out1), .in1({32{1'b0}}), .in2(remainder_out3), .in3(remainder_out4), .out(remainder_out),
    .sel(priority_encoder_1_out));
  Multiplexer #(.select(2), .width(32), .enable("false")) multiplexer_4 (
    .in0(quotient_out1), .in1({32{1'b0}}), .in2(quotient_out3), .in3(quotient_out4), .out(quotient_out),
    .sel(priority_encoder_1_out));
  assign bit_extender_2_out = {{30{1'b0}}, quotient[31:30]};  // Bit_Extender bit_extender_2
  Priority_Encoder #(.select(2)) priority_encoder_2 (
    .in0(1'b1), .in1(not_3_out), .in2(nor_1_out), .in3(nor_2_out), .out(priority_encoder_2_out));  // open: gs, en_out, en_in
  Multiplexer #(.select(2), .width(32), .enable("false")) multiplexer_5 (
    .in0(remainder), .in1(subtractor_1_out), .in2(subtractor_2_out), .in3(subtractor_3_out),
    .out(multiplexer_5_out), .sel(priority_encoder_2_out));
  assign bit_extender_3_out = {{30{1'b0}}, priority_encoder_2_out};  // Bit_Extender bit_extender_3
  Shifter #(.width(32)) shifter_5 (.in(multiplexer_5_out), .\dist (5'b00010), .out(shifter_5_out));
  assign or_1_out = shifter_5_out | bit_extender_2_out;  // OR_Gate or_1, 32 bits wide
  Comparator #(.width(6)) comparator_9 (.a(6'b011110), .b(cnt), .eq(comparator_9_eq));  // open: gt, lt
  assign quotient_out3 = bit_extender_3_out | shifter_4_out;  // OR_Gate or_2, 32 bits wide
  Multiplexer #(.width(32), .enable("false")) multiplexer_6 (
    .in0(or_1_out), .in1(multiplexer_5_out), .out(remainder_out3), .sel(comparator_9_eq));
endmodule

module ALU_divres_end (
  input  [1:0] state,
  input  div_start,
  input  [31:0] remainder,
  input  [31:0] quotient,
  output en,
  output ready_out,
  output [31:0] divres_hi,
  output [31:0] divres_lo
);

  Comparator #(.width(2)) comparator_1 (.a(2'b11), .b(state), .eq(en));  // open: gt, lt
  Multiplexer #(.width(32), .enable("false")) multiplexer_1 (
    .in0({32{1'b0}}), .in1(remainder), .out(divres_hi), .sel(div_start));
  Multiplexer #(.width(32), .enable("false")) multiplexer_2 (
    .in0({32{1'b0}}), .in1(quotient), .out(divres_lo), .sel(div_start));
  Multiplexer #(.enable("false")) multiplexer_3 (.in0(1'b0), .in1(1'b1), .out(ready_out), .sel(div_start));
endmodule

module MCU (
  input  [31:0] maddr,
  input  [7:0] aluop,
  output [3:0] dre,
  output [3:0] we,
  output dce
);

  wire equal8_1_eq, equal8_2_eq, equal8_3_eq, equal8_4_eq;
  wire [1:0] bitselector_1_out;

  BitSelector #(.width(32), .group(2)) bitselector_1 (.in(maddr), .out(bitselector_1_out), .sel(4'b0000));
  MCU_dre mcu_dre_1 (.maddr2(bitselector_1_out), .aluop(aluop), .dre(dre));
  MCU_we mcu_we_1 (.maddr2(bitselector_1_out), .aluop(aluop), .we(we));
  Equal8 equal8_1 (.a(aluop), .b(8'h90), .eq(equal8_1_eq));
  Equal8 equal8_2 (.a(aluop), .b(8'h92), .eq(equal8_2_eq));
  Equal8 equal8_3 (.a(aluop), .b(8'h98), .eq(equal8_3_eq));
  Equal8 equal8_4 (.a(aluop), .b(8'h9a), .eq(equal8_4_eq));
  or or_1 (dce, equal8_1_eq, equal8_2_eq, equal8_3_eq, equal8_4_eq);
endmodule

module MCU_dre (
  input  [1:0] maddr2,
  input  [7:0] aluop,
  output [3:0] dre
);

  wire and_1_out, and_2_out, and_3_out, and_4_out, equal2_1_eq, equal2_2_eq, equal2_3_eq, equal2_4_eq,
       equal8_1_eq, equal8_2_eq;

  Equal2 equal2_1 (.a(maddr2), .b(2'b11), .eq(equal2_1_eq));
  Equal2 equal2_2 (.a(maddr2), .b(2'b10), .eq(equal2_2_eq));
  Equal2 equal2_3 (.a(maddr2), .b(2'b01), .eq(equal2_3_eq));
  Equal2 equal2_4 (.a(maddr2), .b(2'b00), .eq(equal2_4_eq));
  Equal8 equal8_1 (.a(aluop), .b(8'h90), .eq(equal8_1_eq));
  Equal8 equal8_2 (.a(aluop), .b(8'h92), .eq(equal8_2_eq));
  and and_1 (and_1_out, equal2_1_eq, equal8_1_eq);
  and and_2 (and_2_out, equal2_2_eq, equal8_1_eq);
  and and_3 (and_3_out, equal2_3_eq, equal8_1_eq);
  and and_4 (and_4_out, equal2_4_eq, equal8_1_eq);
  or or_1 (dre[0], and_1_out, equal8_2_eq);
  or or_2 (dre[1], and_2_out, equal8_2_eq);
  or or_3 (dre[2], and_3_out, equal8_2_eq);
  or or_4 (dre[3], and_4_out, equal8_2_eq);
endmodule

module MCU_we (
  input  [1:0] maddr2,
  input  [7:0] aluop,
  output [3:0] we
);

  wire and_1_out, and_2_out, and_3_out, and_4_out, equal2_1_eq, equal2_2_eq, equal2_3_eq, equal2_4_eq,
       equal8_1_eq, equal8_2_eq;

  Equal2 equal2_1 (.a(maddr2), .b(2'b11), .eq(equal2_1_eq));
  Equal2 equal2_2 (.a(maddr2), .b(2'b10), .eq(equal2_2_eq));
  Equal2 equal2_3 (.a(maddr2), .b(2'b01), .eq(equal2_3_eq));
  Equal2 equal2_4 (.a(maddr2), .b(2'b00), .eq(equal2_4_eq));
  Equal8 equal8_1 (.a(aluop), .b(8'h98), .eq(equal8_1_eq));
  Equal8 equal8_2 (.a(aluop), .b(8'h9a), .eq(equal8_2_eq));
  and and_1 (and_1_out, equal2_1_eq, equal8_1_eq);
  and and_2 (and_2_out, equal2_2_eq, equal8_1_eq);
  and and_3 (and_3_out, equal2_3_eq, equal8_1_eq);
  and and_4 (and_4_out, equal2_4_eq, equal8_1_eq);
  or or_1 (we[0], and_1_out, equal8_2_eq);
  or or_2 (we[1], and_2_out, equal8_2_eq);
  or or_3 (we[2], and_3_out, equal8_2_eq);
  or or_4 (we[3], and_4_out, equal8_2_eq);
endmodule

module SCU (
  input  stallreq_id,
  input  stallreq_exe,
  output [3:0] stall
);

  wire comparator_1_eq, comparator_2_eq;
  wire [1:0] priority_encoder_1_out;

  Comparator #(.width(1), .mode("unsigned")) comparator_1 (
    .a(stallreq_id), .b(1'b1), .eq(comparator_1_eq));  // open: gt, lt
  Comparator #(.width(1), .mode("unsigned")) comparator_2 (
    .a(stallreq_exe), .b(1'b1), .eq(comparator_2_eq));  // open: gt, lt
  Priority_Encoder #(.select(2)) priority_encoder_1 (
    .in0(1'b1), .in1(comparator_1_eq), .in2(comparator_2_eq), .out(priority_encoder_1_out));  // open: in3, gs, en_out, en_in
  Multiplexer #(.select(2), .width(4), .enable("false")) multiplexer_1 (
    .in0(4'b0000), .in1(4'b0111), .in2(4'b1111), .out(stall), .sel(priority_encoder_1_out));  // open: in3
endmodule

module EqualMux (
  input  [31:0] src,
  input  [7:0] en1,
  input  [7:0] en2,
  output [31:0] out_4
);

  wire nor_1_out;
  wire [7:0] xor_1_out;

  assign xor_1_out = en1 ^ en2;  // XOR_Gate xor_1, 8 bits wide
  Multiplexer #(.width(32), .enable("false")) multiplexer_1 (.in0({32{1'b0}}), .in1(src), .out(out_4), .sel(nor_1_out));
  nor nor_1 (nor_1_out, xor_1_out[0], xor_1_out[1], xor_1_out[2], xor_1_out[3], xor_1_out[4], xor_1_out[5], xor_1_out[6], xor_1_out[7]);
endmodule

module TrueMux6 (
  input  in_1,
  input  [5:0] in_2,
  output [5:0] out_3
);

  Multiplexer #(.width(6), .enable("false")) multiplexer_1 (.in0({6{1'b0}}), .in1(in_2), .out(out_3), .sel(in_1));
endmodule

module TrueMux2 (
  input  in_1,
  input  [1:0] in_2,
  output [1:0] out_3
);

  Multiplexer #(.width(2), .enable("false")) multiplexer_1 (.in0(2'b00), .in1(in_2), .out(out_3), .sel(in_1));
endmodule

module Equal8 (
  input  [7:0] a,
  input  [7:0] b,
  output eq
);

  wire [7:0] xor_1_out;

  assign xor_1_out = a ^ b;  // XOR_Gate xor_1, 8 bits wide
  nor nor_1 (eq, xor_1_out[0], xor_1_out[1], xor_1_out[2], xor_1_out[3], xor_1_out[4], xor_1_out[5], xor_1_out[6], xor_1_out[7]);
endmodule

module Equal2 (
  input  [1:0] a,
  input  [1:0] b,
  output eq
);

  wire [1:0] xor_1_out;

  assign xor_1_out = a ^ b;  // XOR_Gate xor_1, 2 bits wide
  nor nor_1 (eq, xor_1_out[0], xor_1_out[1]);
endmodule
